// Logisim project ComputerArchitecture.circ as structural Verilog: 21 circuits, main circuit fourbit
module fourbit (
  input  [3:0] Ain,
  input  [3:0] Bin,
  output [3:0] Sum,
  output Co
);

  wire fulladder_1_cout, fulladder_2_cout, halfadder_1_cout;

  halfadder halfadder_1 (.InputA(Ain[0]), .InputB(Bin[0]), .numout(Sum[0]), .Cout(halfadder_1_cout));
  fulladder fulladder_1 (.Cin(halfadder_1_cout), .A(Ain[1]), .B(Bin[1]), .numout(Sum[1]), .Cout(fulladder_1_cout));
  fulladder fulladder_2 (.Cin(fulladder_1_cout), .A(Ain[2]), .B(Bin[2]), .numout(Sum[2]), .Cout(fulladder_2_cout));
  fulladder fulladder_3 (.Cin(fulladder_2_cout), .A(Ain[3]), .B(Bin[3]), .numout(Sum[3]), .Cout(Co));
endmodule

module fulladder (
  input  Cin,
  input  A,
  input  B,
  output numout,
  output Cout
);

  wire and_1_out, and_2_out, xor_1_out;

  xor xor_1 (xor_1_out, A, B);
  and and_1 (and_1_out, A, B);
  xor xor_2 (numout, Cin, xor_1_out);
  and and_2 (and_2_out, Cin, xor_1_out);
  or or_1 (Cout, and_2_out, and_1_out);
endmodule

module halfadder (
  input  InputA,
  input  InputB,
  output numout,
  output Cout
);

  xor xor_1 (numout, InputA, InputB);
  and and_1 (Cout, InputA, InputB);
endmodule

module main (
  input  in_1,
  input  in_2,
  input  Reset,
  input  Clk,
  input  writeEnable,
  input  in_6,
  input  in_7,
  input  ReadEnable,
  input  in_9,
  input  in_10,
  input  in_11,
  input  in_12,
  input  in_13,
  input  in_14,
  input  in_15,
  input  in_16,
  input  in_17,
  input  in_18,
  input  in_19,
  input  in_20,
  input  in_21
);

  wire button_1_out, LOAD_out, MEM0_serout, MEM1_serout, MEM2_serout, MEM3_serout, minimux_1_dout,
       mydemux_1_d0, mydemux_1_d1, mydemux_1_d2, mydemux_1_d3, mydemux_2_d0, mydemux_2_d1, mydemux_2_d2,
       mydemux_2_d3, mydemux_3_d0, mydemux_3_d1, mydemux_3_d2, mydemux_3_d3, mydemux_4_d0, mydemux_4_d1,
       mydemux_4_d2, mydemux_4_d3, mydemux_5_d0, mydemux_5_d1, mydemux_5_d2, mydemux_5_d3, parser_1_do,
       SOURCE_dout;
  wire [1:0] count_1_cout, count_2_cout, undriven;
  wire [3:0] demux4_1_d0, demux4_1_d1, demux4_1_d2, demux4_1_d3, fourbit_1_sum, MEM0_parout, MEM1_parout,
       MEM2_parout, MEM3_parout, memcell_1_parout, memcell_2_parout, memcell_3_parout, memcell_4_parout,
       mux4_1_dout, mux4_2_dout, REG0_parout, REG1_parout, REG2_parout, REG3_parout;

  Button LOAD (.out(LOAD_out));
  mydemux mydemux_1 (
    .Enable(1'b1), .C0(count_1_cout[0]), .C1(count_1_cout[1]), .Din(LOAD_out), .D0(mydemux_1_d0),
    .D1(mydemux_1_d1), .D2(mydemux_1_d2), .D3(mydemux_1_d3));
  count count_1 (.Clk(LOAD_out), .Cout(count_1_cout));  // open: Reset
  mydemux mydemux_2 (
    .Enable(ReadEnable), .C0(in_10), .C1(in_9), .Din(ReadEnable), .D0(mydemux_2_d0), .D1(mydemux_2_d1),
    .D2(mydemux_2_d2), .D3(mydemux_2_d3));
  Hex_Digit_Display hex_digit_display_1 (.value(MEM0_parout));  // open: dp
  Hex_Digit_Display hex_digit_display_2 (.value(MEM1_parout));  // open: dp
  Hex_Digit_Display hex_digit_display_3 (.value(MEM2_parout));  // open: dp
  Hex_Digit_Display hex_digit_display_4 (.value(MEM3_parout));  // open: dp
  memcell MEM0 (
    .Parlin({in_15, in_16, in_17, in_18}), .Load(mydemux_1_d0), .Read(mydemux_2_d0), .SerOut(MEM0_serout),
    .ParOut(MEM0_parout));  // open: Serin, Write
  memcell MEM1 (
    .Parlin({in_15, in_16, in_17, in_18}), .Load(mydemux_1_d1), .Read(mydemux_2_d1), .SerOut(MEM1_serout),
    .ParOut(MEM1_parout));  // open: Serin, Write
  memcell MEM2 (
    .Parlin({in_15, in_16, in_17, in_18}), .Load(mydemux_1_d2), .Read(mydemux_2_d2), .SerOut(MEM2_serout),
    .ParOut(MEM2_parout));  // open: Serin, Write
  memcell MEM3 (
    .Parlin({in_15, in_16, in_17, in_18}), .Load(mydemux_1_d3), .Read(mydemux_2_d3), .SerOut(MEM3_serout),
    .ParOut(MEM3_parout));  // open: Serin, Write
  minimux SOURCE (
    .C0(in_10), .C1(in_9), .D0(MEM0_serout), .D1(MEM1_serout), .D2(MEM2_serout), .D3(MEM3_serout),
    .Dout(SOURCE_dout));
  minimux minimux_1 (
    .C0(ReadEnable), .C1(in_19), .D0(parser_1_do), .D1(SOURCE_dout), .Dout(minimux_1_dout));  // open: D2, D3
  mydemux mydemux_3 (
    .Enable(writeEnable), .C0(in_7), .C1(in_6), .Din(minimux_1_dout), .D0(mydemux_3_d0), .D1(mydemux_3_d1),
    .D2(mydemux_3_d2), .D3(mydemux_3_d3));
  mydemux mydemux_4 (
    .Enable(writeEnable), .C0(in_7), .C1(in_6), .Din(writeEnable), .D0(mydemux_4_d0), .D1(mydemux_4_d1),
    .D2(mydemux_4_d2), .D3(mydemux_4_d3));
  Clock clock_1 ();  // open: out
  Hex_Digit_Display hex_digit_display_5 (.value(REG0_parout));  // open: dp
  Hex_Digit_Display hex_digit_display_6 (.value(REG1_parout));  // open: dp
  Hex_Digit_Display hex_digit_display_7 (.value(REG2_parout));  // open: dp
  Hex_Digit_Display hex_digit_display_8 (.value(REG3_parout));  // open: dp
  memcell REG0 (.Serin(mydemux_3_d0), .Write(mydemux_4_d0), .ParOut(REG0_parout));  // open: Parlin, Load, Read, SerOut
  memcell REG1 (.Serin(mydemux_3_d1), .Write(mydemux_4_d1), .ParOut(REG1_parout));  // open: Parlin, Load, Read, SerOut
  memcell REG2 (.Serin(mydemux_3_d2), .Write(mydemux_4_d2), .ParOut(REG2_parout));  // open: Parlin, Load, Read, SerOut
  memcell REG3 (.Serin(mydemux_3_d3), .Write(mydemux_4_d3), .ParOut(REG3_parout));  // open: Parlin, Load, Read, SerOut
  Hex_Digit_Display hex_digit_display_9 (.value(fourbit_1_sum));  // open: dp
  mux4 mux4_1 (
    .C0(count_2_cout[0]), .C1(count_2_cout[1]), .D0(REG0_parout), .D1(REG1_parout), .D2(REG2_parout),
    .D3(REG3_parout), .Dout(mux4_1_dout));
  mux4 mux4_2 (
    .C0(in_21), .C1(in_20), .D0(REG0_parout), .D1(REG1_parout), .D2(REG2_parout), .D3(REG3_parout),
    .Dout(mux4_2_dout));
  Button button_1 (.out(button_1_out));
  fourbit fourbit_1 (.Ain(mux4_1_dout), .Bin(mux4_2_dout), .Sum(fourbit_1_sum));  // open: Co
  mydemux mydemux_5 (
    .Enable(1'b1), .C0(count_2_cout[0]), .C1(count_2_cout[1]), .Din(button_1_out), .D0(mydemux_5_d0),
    .D1(mydemux_5_d1), .D2(mydemux_5_d2), .D3(mydemux_5_d3));
  demux4 demux4_1 (
    .CP0(count_2_cout[0]), .CP1(count_2_cout[1]), .Din(fourbit_1_sum), .D0(demux4_1_d0), .D1(demux4_1_d1),
    .D2(demux4_1_d2), .D3(demux4_1_d3));
  Hex_Digit_Display hex_digit_display_10 (.value(memcell_1_parout));  // open: dp
  Hex_Digit_Display hex_digit_display_11 (.value(memcell_2_parout));  // open: dp
  Hex_Digit_Display hex_digit_display_12 (.value(memcell_3_parout));  // open: dp
  Hex_Digit_Display hex_digit_display_13 (.value(memcell_4_parout));  // open: dp
  count count_2 (.Clk(Clk), .Reset(Reset), .Cout(count_2_cout));
  memcell memcell_1 (
    .Parlin(demux4_1_d0), .Load(mydemux_5_d0), .ParOut(memcell_1_parout));  // open: Serin, Read, Write, SerOut
  memcell memcell_2 (
    .Parlin(demux4_1_d1), .Load(mydemux_5_d1), .ParOut(memcell_2_parout));  // open: Serin, Read, Write, SerOut
  memcell memcell_3 (
    .Parlin(demux4_1_d2), .Load(mydemux_5_d2), .ParOut(memcell_3_parout));  // open: Serin, Read, Write, SerOut
  memcell memcell_4 (
    .Parlin(demux4_1_d3), .Load(mydemux_5_d3), .ParOut(memcell_4_parout));  // open: Serin, Read, Write, SerOut
  Hex_Digit_Display hex_digit_display_14 (.value({in_13, in_14, undriven}));  // open: dp
  parser parser_1 (.Din(fourbit_1_sum), .Do(parser_1_do));

  // Notes on the sheet:
  //   ADDRESS
  //   VALUE
  //   RAM
  //   SOURCE
  //   Destination
  //   ALU vs MEM
  //   redundant
  //   It needs 8 bits to register from the sum as first four bits clear the previous value and then the next four bits inserts the sum value or output. But if you want the change in just 4 bits then remove the redundant mydemux circuit and then connect the Dout the minimux to all the serial inputs of the memory cells
  //   CPU
  //   ALU
  //   ADD
endmodule

module mymux (
  input  A1,
  input  A0,
  input  [3:0] Din,
  output Dout
);

  wire and_1_out, and_2_out, and_3_out, and_4_out, and_5_out, and_6_out, and_7_out, nor_1_out, not_1_out,
       not_2_out;

  nor nor_1 (nor_1_out, A0, A1);
  and and_1 (and_1_out, A0, not_1_out);
  not not_1 (not_1_out, A1);
  not not_2 (not_2_out, A0);
  and and_2 (and_2_out, not_2_out, A1);
  and and_3 (and_3_out, A0, A1);
  and and_4 (and_4_out, nor_1_out, Din[0]);
  and and_5 (and_5_out, Din[1], and_1_out);
  and and_6 (and_6_out, and_2_out, Din[2]);
  and and_7 (and_7_out, Din[3], and_3_out);
  or or_1 (Dout, and_4_out, and_5_out, and_6_out, and_7_out);
endmodule

module minimux (
  input  C0,
  input  C1,
  input  D0,
  input  D1,
  input  D2,
  input  D3,
  output Dout
);

  wire and_1_out, and_2_out, and_3_out, and_4_out, not_1_out, not_2_out, not_3_out, not_4_out;

  not not_1 (not_1_out, C0);
  not not_2 (not_2_out, C1);
  not not_3 (not_3_out, C1);
  not not_4 (not_4_out, C0);
  and and_1 (and_1_out, not_1_out, not_2_out, D0);
  and and_2 (and_2_out, not_3_out, C0, D1);
  and and_3 (and_3_out, C1, not_4_out, D2);
  and and_4 (and_4_out, C1, C0, D3);
  or or_1 (Dout, and_1_out, and_2_out, and_3_out, and_4_out);
endmodule

module mux4 (
  input  C0,
  input  C1,
  input  [3:0] D0,
  input  [3:0] D1,
  input  [3:0] D2,
  input  [3:0] D3,
  output [3:0] Dout
);

  minimux minimux_1 (.C0(C0), .C1(C1), .D0(D0[0]), .D1(D1[0]), .D2(D2[0]), .D3(D3[0]), .Dout(Dout[0]));
  minimux minimux_2 (.C0(C0), .C1(C1), .D0(D0[1]), .D1(D1[1]), .D2(D2[1]), .D3(D3[1]), .Dout(Dout[1]));
  minimux minimux_3 (.C0(C0), .C1(C1), .D0(D0[2]), .D1(D1[2]), .D2(D2[2]), .D3(D3[2]), .Dout(Dout[2]));
  minimux minimux_4 (.C0(C0), .C1(C1), .D0(D0[3]), .D1(D1[3]), .D2(D2[3]), .D3(D3[3]), .Dout(Dout[3]));
endmodule

module mydemux (
  input  Enable,
  input  C0,
  input  C1,
  input  Din,
  output D0,
  output D1,
  output D2,
  output D3
);

  wire and_1_out, not_1_out, not_2_out, not_3_out, not_4_out;

  and and_1 (and_1_out, Enable, Din);
  not not_1 (not_1_out, C0);
  not not_2 (not_2_out, C1);
  not not_3 (not_3_out, C1);
  not not_4 (not_4_out, C0);
  and and_2 (D0, not_1_out, not_2_out, and_1_out);
  and and_3 (D1, not_3_out, C0, and_1_out);
  and and_4 (D2, C1, not_4_out, and_1_out);
  and and_5 (D3, C1, C0, and_1_out);
endmodule

module memcell (
  input  [3:0] Parlin,
  input  Load,
  input  Serin,
  input  Read,
  input  Write,
  output SerOut,
  output [3:0] ParOut
);

  wire and_1_out, and_2_out, and_3_out, and_4_out, and_5_out, and_6_out, and_7_out, and_8_out, and_9_out,
       and_10_out, and_11_out, and_12_out, and_13_out, and_14_out, and_15_out, and_16_out, and_17_out,
       and_18_out, clock_1_out, clock_2_out, clock_3_out, clock_4_out, not_1_out, not_2_out, not_3_out,
       not_4_out, not_5_out, not_6_out, not_7_out, not_8_out, or_1_out, or_2_out;

  and and_1 (and_1_out, Write, Serin);
  and and_2 (and_2_out, ParOut[3], Read);
  or or_1 (or_1_out, Write, Read);
  or or_2 (or_2_out, and_1_out, and_2_out);
  not not_1 (not_1_out, or_2_out);
  and and_3 (and_3_out, or_1_out, or_2_out);
  and and_4 (and_4_out, or_1_out, not_1_out);
  J_K_Flip_Flop j_k_ff_1 (
    .J(and_3_out), .K(and_4_out), .clk(clock_1_out), .Q(ParOut[0]), .preset(and_5_out), .reset(and_6_out));  // open: Qn
  Clock clock_1 (.out(clock_1_out));
  and and_5 (and_5_out, Load, Parlin[0]);
  and and_6 (and_6_out, Load, not_2_out);
  not not_2 (not_2_out, Parlin[0]);
  and and_7 (and_7_out, or_1_out, ParOut[0]);
  and and_8 (and_8_out, or_1_out, not_3_out);
  not not_3 (not_3_out, ParOut[0]);
  Clock clock_2 (.out(clock_2_out));
  and and_9 (and_9_out, Load, Parlin[1]);
  J_K_Flip_Flop j_k_ff_2 (
    .J(and_7_out), .K(and_8_out), .clk(clock_2_out), .Q(ParOut[1]), .preset(and_9_out), .reset(and_10_out));  // open: Qn
  and and_10 (and_10_out, Load, not_4_out);
  not not_4 (not_4_out, Parlin[1]);
  and and_11 (and_11_out, or_1_out, ParOut[1]);
  and and_12 (and_12_out, or_1_out, not_5_out);
  not not_5 (not_5_out, ParOut[1]);
  Clock clock_3 (.out(clock_3_out));
  J_K_Flip_Flop j_k_ff_3 (
    .J(and_11_out), .K(and_12_out), .clk(clock_3_out), .Q(ParOut[2]), .preset(and_13_out), .reset(and_14_out));  // open: Qn
  and and_13 (and_13_out, Load, Parlin[2]);
  and and_14 (and_14_out, Load, not_6_out);
  not not_6 (not_6_out, Parlin[2]);
  and and_15 (and_15_out, or_1_out, ParOut[2]);
  and and_16 (and_16_out, or_1_out, not_7_out);
  not not_7 (not_7_out, ParOut[2]);
  Clock clock_4 (.out(clock_4_out));
  and and_17 (and_17_out, Load, Parlin[3]);
  J_K_Flip_Flop j_k_ff_4 (
    .J(and_15_out), .K(and_16_out), .clk(clock_4_out), .Q(ParOut[3]), .preset(and_17_out), .reset(and_18_out));  // open: Qn
  and and_18 (and_18_out, Load, not_8_out);
  not not_8 (not_8_out, Parlin[3]);

  assign SerOut = ParOut[3];
endmodule

module demux4 (
  input  CP0,
  input  CP1,
  input  [3:0] Din,
  output [3:0] D0,
  output [3:0] D1,
  output [3:0] D2,
  output [3:0] D3
);

  mydemux mydemux_1 (.Enable(1'b1), .C0(CP0), .C1(CP1), .Din(Din[0]), .D0(D0[0]), .D1(D1[0]), .D2(D2[0]), .D3(D3[0]));
  mydemux mydemux_2 (.Enable(1'b1), .C0(CP0), .C1(CP1), .Din(Din[1]), .D0(D0[1]), .D1(D1[1]), .D2(D2[1]), .D3(D3[1]));
  mydemux mydemux_3 (.Enable(1'b1), .C0(CP0), .C1(CP1), .Din(Din[2]), .D0(D0[2]), .D1(D1[2]), .D2(D2[2]), .D3(D3[2]));
  mydemux mydemux_4 (.Enable(1'b1), .C0(CP0), .C1(CP1), .Din(Din[3]), .D0(D0[3]), .D1(D1[3]), .D2(D2[3]), .D3(D3[3]));
endmodule

module count (
  input  Clk,
  input  Reset,
  output [1:0] Cout
);

  wire and_1_out, or_1_out, t_ff_1_q, t_ff_2_q, t_ff_3_q;

  T_Flip_Flop t_ff_1 (.T(1'b1), .clk(Clk), .Q(t_ff_1_q), .reset(or_1_out));  // open: Qn, preset
  D_Flip_Flop #(.trigger("falling")) d_ff_1 (.D(t_ff_1_q), .clk(Clk), .Q(Cout[0]), .reset(Reset));  // open: Qn, preset
  T_Flip_Flop t_ff_2 (.T(t_ff_1_q), .clk(Clk), .Q(t_ff_2_q), .reset(or_1_out));  // open: Qn, preset
  D_Flip_Flop #(.trigger("falling")) d_ff_2 (.D(t_ff_2_q), .clk(Clk), .Q(Cout[1]), .reset(Reset));  // open: Qn, preset
  and and_1 (and_1_out, t_ff_1_q, t_ff_2_q);
  T_Flip_Flop t_ff_3 (.T(and_1_out), .clk(Clk), .Q(t_ff_3_q), .reset(or_1_out));  // open: Qn, preset
  or or_1 (or_1_out, t_ff_3_q, Reset);
endmodule

module parser (
  input  [3:0] Din,
  output Do
);

  wire clock_1_out;
  wire [1:0] count_1_cout;

  Clock clock_1 (.out(clock_1_out));
  count count_1 (.Clk(clock_1_out), .Cout(count_1_cout));  // open: Reset
  minimux minimux_1 (
    .C0(count_1_cout[0]), .C1(count_1_cout[1]), .D0(Din[0]), .D1(Din[1]), .D2(Din[2]), .D3(Din[3]), .Dout(Do));
endmodule

module Computer (
  input  in_1,
  input  in_2,
  input  in_3,
  input  in_4
);

  wire and_1_out, and_2_out, and_3_out, and_4_out, button_1_out, decoder_1_out0, decoder_1_out1,
       decoder_2_out0, decoder_2_out1, decoder_2_out2, decoder_2_out3, decoder_3_out0, decoder_3_out1,
       decoder_3_out2, decoder_3_out3, decoder_4_out0, decoder_4_out1, decoder_4_out2, decoder_4_out3,
       fourbit2_1_vo, LOAD_out, memcell_1_serout, memcell_2_serout, memcell_3_serout, memcell_4_serout,
       multiplexer_1_out, mydemux_1_d0, mydemux_1_d1, mydemux_1_d2, mydemux_1_d3, not_1_out, not_2_out,
       not_3_out, or_1_out, parser_1_do, ReadingtoMem_d0, ReadingtoMem_d1, ReadingtoMem_d2, ReadingtoMem_d3,
       WritingToMem_d0, WritingToMem_d1, WritingToMem_d2, WritingToMem_d3;
  wire [1:0] count_1_cout, PC_dout_2, PC_dout_3, PC_dout_4, PC_dout_5;
  wire [2:0] or_3_out;
  wire [3:0] fourbit2_1_r0, memcell_1_parout, memcell_2_parout, memcell_3_parout, memcell_4_parout,
       memcell_5_parout, memcell_6_parout, memcell_7_parout, memcell_8_parout, multiplexer_2_out,
       multiplexer_3_out, multiplexer_4_out, multiplexer_5_out, PC_count;
  wire [11:8] PC_dout;

  Button LOAD (.out(LOAD_out));
  count count_1 (.Clk(LOAD_out), .Cout(count_1_cout));  // open: Reset
  mydemux ReadingtoMem (
    .Enable(decoder_1_out1), .C0(PC_dout_2[0]), .C1(PC_dout_2[1]), .Din(1'b1), .D0(ReadingtoMem_d0),
    .D1(ReadingtoMem_d1), .D2(ReadingtoMem_d2), .D3(ReadingtoMem_d3));
  mydemux WritingToMem (
    .Enable(decoder_1_out0), .C0(PC_dout_2[0]), .C1(PC_dout_2[1]), .Din(1'b1), .D0(WritingToMem_d0),
    .D1(WritingToMem_d1), .D2(WritingToMem_d2), .D3(WritingToMem_d3));
  Button button_1 (.out(button_1_out));
  mydemux mydemux_1 (
    .Enable(1'b1), .C0(count_1_cout[0]), .C1(count_1_cout[1]), .Din(LOAD_out), .D0(mydemux_1_d0),
    .D1(mydemux_1_d1), .D2(mydemux_1_d2), .D3(mydemux_1_d3));
  Hex_Digit_Display hex_digit_display_1 (.value(PC_count));  // open: dp
  Fetcher PC (
    .RST(button_1_out), .num0(12'hc10), .num1(12'h240), .num2(12'h34a), .num3(12'h4c4), .count(PC_count),
    .Dout({PC_dout, PC_dout_3, PC_dout_2, PC_dout_5, PC_dout_4}));  // open: N, num4, num5, num6, num7
  Decoder decoder_1 (.out0(decoder_1_out0), .out1(decoder_1_out1), .sel(PC_dout[10]), .en(PC_dout[11]));
  and and_1 (and_1_out, PC_dout[11], PC_dout[10]);
  Hex_Digit_Display hex_digit_display_2 (.value(memcell_1_parout));  // open: dp
  Hex_Digit_Display hex_digit_display_3 (.value(memcell_2_parout));  // open: dp
  Hex_Digit_Display hex_digit_display_4 (.value(memcell_3_parout));  // open: dp
  Hex_Digit_Display hex_digit_display_5 (.value(memcell_4_parout));  // open: dp
  memcell memcell_1 (
    .Parlin({in_1, in_2, in_3, in_4}), .Load(mydemux_1_d0), .Serin(parser_1_do), .Read(ReadingtoMem_d0),
    .Write(WritingToMem_d0), .SerOut(memcell_1_serout), .ParOut(memcell_1_parout));
  memcell memcell_2 (
    .Parlin({in_1, in_2, in_3, in_4}), .Load(mydemux_1_d1), .Serin(parser_1_do), .Read(ReadingtoMem_d1),
    .Write(WritingToMem_d1), .SerOut(memcell_2_serout), .ParOut(memcell_2_parout));
  memcell memcell_3 (
    .Parlin({in_1, in_2, in_3, in_4}), .Load(mydemux_1_d2), .Serin(parser_1_do), .Read(ReadingtoMem_d2),
    .Write(WritingToMem_d2), .SerOut(memcell_3_serout), .ParOut(memcell_3_parout));
  memcell memcell_4 (
    .Parlin({in_1, in_2, in_3, in_4}), .Load(mydemux_1_d3), .Serin(parser_1_do), .Read(ReadingtoMem_d3),
    .Write(WritingToMem_d3), .SerOut(memcell_4_serout), .ParOut(memcell_4_parout));
  Clock clock_1 ();  // open: out
  Multiplexer #(.select(2)) multiplexer_1 (
    .in0(memcell_1_serout), .in1(memcell_2_serout), .in2(memcell_3_serout), .in3(memcell_4_serout),
    .out(multiplexer_1_out), .sel(PC_dout_2));
  parser parser_1 (.Din(multiplexer_4_out), .Do(parser_1_do));
  not not_1 (not_1_out, PC_dout[11]);
  and and_2 (and_2_out, not_1_out, PC_dout[10]);
  or or_1 (or_1_out, PC_dout[9], and_2_out);
  Decoder #(.select(2)) decoder_2 (
    .out0(decoder_2_out0), .out1(decoder_2_out1), .out2(decoder_2_out2), .out3(decoder_2_out3),
    .sel(PC_dout_3), .en(or_1_out));
  not not_2 (not_2_out, PC_dout[10]);
  and and_3 (and_3_out, PC_dout[11], not_2_out);
  Decoder #(.select(2)) decoder_3 (
    .out0(decoder_3_out0), .out1(decoder_3_out1), .out2(decoder_3_out2), .out3(decoder_3_out3),
    .sel(PC_dout_2), .en(and_3_out));
  Decoder #(.select(2)) decoder_4 (
    .out0(decoder_4_out0), .out1(decoder_4_out1), .out2(decoder_4_out2), .out3(decoder_4_out3),
    .sel(PC_dout_3), .en(and_1_out));
  Multiplexer #(.select(3), .width(4)) multiplexer_2 (
    .in0(memcell_5_parout), .in1(memcell_6_parout), .in2(memcell_7_parout), .in3(memcell_8_parout),
    .in4({PC_dout_5, PC_dout_4}), .out(multiplexer_2_out), .sel({1'b0, PC_dout_2}));  // open: in5, in6, in7
  LED led_1 (.in(fourbit2_1_r0[0]));
  LED led_2 (.in(fourbit2_1_r0[1]));
  LED led_3 (.in(fourbit2_1_r0[2]));
  not not_3 (not_3_out, PC_dout[11]);
  LED led_4 (.in(fourbit2_1_vo));
  fourbit2 fourbit2_1 (
    .Ain(multiplexer_3_out), .Bin(multiplexer_2_out), .Vo(fourbit2_1_vo), .R3(fourbit2_1_r0[3]),
    .R2(fourbit2_1_r0[2]), .R1(fourbit2_1_r0[1]), .R0(fourbit2_1_r0[0]));
  LED led_5 (.in(fourbit2_1_r0[3]));
  and and_4 (and_4_out, PC_dout[10], not_3_out);
  or or_2 (or_3_out[2], and_4_out, PC_dout[8]);
  Multiplexer #(.select(3), .width(4)) multiplexer_3 (
    .in0(memcell_5_parout), .in1(memcell_6_parout), .in2(memcell_7_parout), .in3(memcell_8_parout),
    .in4({PC_dout_5, PC_dout_4}), .out(multiplexer_3_out), .sel({1'b0, PC_dout_5}));  // open: in5, in6, in7
  Multiplexer #(.select(3), .width(4)) multiplexer_4 (
    .in0(memcell_5_parout), .in1(memcell_6_parout), .in2(memcell_7_parout), .in3(memcell_8_parout),
    .in4(fourbit2_1_r0), .out(multiplexer_4_out));  // open: in5, in6, in7, sel
  or or_3 (or_3_out[0], and_4_out, PC_dout_2[0]);
  Hex_Digit_Display hex_digit_display_6 (.value(memcell_5_parout));  // open: dp
  Hex_Digit_Display hex_digit_display_7 (.value(memcell_6_parout));  // open: dp
  Hex_Digit_Display hex_digit_display_8 (.value(memcell_7_parout));  // open: dp
  Hex_Digit_Display hex_digit_display_9 (.value(memcell_8_parout));  // open: dp
  Multiplexer #(.select(3), .width(4)) multiplexer_5 (
    .in0(memcell_5_parout), .in1(memcell_6_parout), .in2(memcell_7_parout), .in3(memcell_8_parout),
    .in4({PC_dout_5, PC_dout_4}), .in5(fourbit2_1_r0), .out(multiplexer_5_out),
    .sel({or_3_out[2], PC_dout_2[1], or_3_out[0]}));  // open: in6, in7
  memcell memcell_5 (
    .Parlin(multiplexer_5_out), .Load(decoder_2_out0), .Serin(multiplexer_1_out), .Read(decoder_3_out0),
    .Write(decoder_4_out0), .ParOut(memcell_5_parout));  // open: SerOut
  memcell memcell_6 (
    .Parlin(multiplexer_5_out), .Load(decoder_2_out1), .Serin(multiplexer_1_out), .Read(decoder_3_out1),
    .Write(decoder_4_out1), .ParOut(memcell_6_parout));  // open: SerOut
  memcell memcell_7 (
    .Parlin(multiplexer_5_out), .Load(decoder_2_out2), .Serin(multiplexer_1_out), .Read(decoder_3_out2),
    .Write(decoder_4_out2), .ParOut(memcell_7_parout));  // open: SerOut
  memcell memcell_8 (
    .Parlin(multiplexer_5_out), .Load(decoder_2_out3), .Serin(multiplexer_1_out), .Read(decoder_3_out3),
    .Write(decoder_4_out3), .ParOut(memcell_8_parout));  // open: SerOut

  // Notes on the sheet:
  //   VALUE
  //   ADDRESS
  //   LDR RX,MY = 1100 XX YY 0000
  //   MOV RX,RY = 0010 XX YY 0000
endmodule

module Fetcher (
  input  N,
  input  RST,
  input  [11:0] num0,
  input  [11:0] num1,
  input  [11:0] num2,
  input  [11:0] num3,
  input  [11:0] num4,
  input  [11:0] num5,
  input  [11:0] num6,
  input  [11:0] num7,
  output [3:0] count,
  output [11:0] Dout
);

  wire clock_1_out;
  wire [1:0] count2_1_cout;

  Clock clock_1 (.out(clock_1_out));
  count2 count2_1 (.Clk(clock_1_out), .Reset(RST), .Cout(count2_1_cout));
  counter0_to_7 counter0_to_7_1 (.Clock(count2_1_cout[1]), .Reset(RST), .out_3(count[2:0]));
  Hex_Digit_Display hex_digit_display_1 (.value({2'b00, count2_1_cout}));  // open: dp
  Hex_Digit_Display hex_digit_display_2 (.value({N, count[2:0]}));  // open: dp
  mux12 mux12_1 (
    .num0(num0), .num1(num1), .num2(num2), .num3(num3), .num4(num4), .num5(num5), .num6(num6), .num7(num7),
    .Controlpins(count[2:0]), .Dout(Dout));

  assign count[3] = N;
endmodule

module mux12 (
  input  [11:0] num0,
  input  [11:0] num1,
  input  [11:0] num2,
  input  [11:0] num3,
  input  [11:0] num4,
  input  [11:0] num5,
  input  [11:0] num6,
  input  [11:0] num7,
  input  [2:0] Controlpins,
  output [11:0] Dout
);

  Multiplexer #(.select(3), .width(12)) multiplexer_1 (
    .in0(num0), .in1(num1), .in2(num2), .in3(num3), .in4(num4), .in5(num5), .in6(num6), .in7(num7),
    .out(Dout), .sel(Controlpins));
endmodule

module counter0_to_7 (
  input  Clock,
  input  Reset,
  output [2:0] out_3
);

  wire and_1_out, and_2_out, or_1_out, t_ff_1_q, t_ff_2_q, t_ff_3_q, t_ff_4_q;

  T_Flip_Flop t_ff_1 (.T(1'b1), .clk(Clock), .Q(t_ff_1_q), .reset(or_1_out));  // open: Qn, preset
  D_Flip_Flop #(.trigger("falling")) d_ff_1 (
    .D(t_ff_1_q), .clk(Clock), .Q(out_3[0]), .reset(Reset));  // open: Qn, preset
  T_Flip_Flop t_ff_2 (.T(t_ff_1_q), .clk(Clock), .Q(t_ff_2_q), .reset(or_1_out));  // open: Qn, preset
  and and_1 (and_1_out, t_ff_1_q, t_ff_2_q);
  T_Flip_Flop t_ff_3 (.T(and_1_out), .clk(Clock), .Q(t_ff_3_q), .reset(or_1_out));  // open: Qn, preset
  D_Flip_Flop #(.trigger("falling")) d_ff_2 (
    .D(t_ff_2_q), .clk(Clock), .Q(out_3[1]), .reset(Reset));  // open: Qn, preset
  and and_2 (and_2_out, and_1_out, t_ff_3_q);
  T_Flip_Flop t_ff_4 (.T(and_2_out), .clk(Clock), .Q(t_ff_4_q), .reset(or_1_out));  // open: Qn, preset
  D_Flip_Flop #(.trigger("falling")) d_ff_3 (
    .D(t_ff_3_q), .clk(Clock), .Q(out_3[2]), .reset(Reset));  // open: Qn, preset
  or or_1 (or_1_out, t_ff_4_q, Reset);
endmodule

module fourbit2 (
  input  [3:0] Ain,
  input  [3:0] Bin,
  output Vo,
  output R3,
  output R2,
  output R1,
  output R0
);

  wire fulladder_1_cout, fulladder_2_cout, halfadder_1_cout;

  halfadder halfadder_1 (.InputA(Ain[0]), .InputB(Bin[0]), .numout(R0), .Cout(halfadder_1_cout));
  fulladder fulladder_1 (.Cin(halfadder_1_cout), .A(Ain[1]), .B(Bin[1]), .numout(R1), .Cout(fulladder_1_cout));
  fulladder fulladder_2 (.Cin(fulladder_1_cout), .A(Ain[2]), .B(Bin[2]), .numout(R2), .Cout(fulladder_2_cout));
  fulladder fulladder_3 (.Cin(fulladder_2_cout), .A(Ain[3]), .B(Bin[3]), .numout(R3), .Cout(Vo));
endmodule

module count2 (
  input  Clk,
  input  Reset,
  output [1:0] Cout
);

  wire and_1_out, or_1_out, t_ff_1_q, t_ff_2_q;

  T_Flip_Flop t_ff_1 (.T(1'b1), .clk(Clk), .Q(t_ff_1_q), .reset(or_1_out));  // open: Qn, preset
  D_Flip_Flop d_ff_1 (.D(t_ff_1_q), .clk(Clk), .Q(Cout[0]), .reset(Reset));  // open: Qn, preset
  T_Flip_Flop t_ff_2 (.T(t_ff_1_q), .clk(Clk), .Q(t_ff_2_q), .reset(or_1_out));  // open: Qn, preset
  D_Flip_Flop d_ff_2 (.D(t_ff_2_q), .clk(Clk), .Q(Cout[1]), .reset(Reset));  // open: Qn, preset
  and and_1 (and_1_out, t_ff_1_q, t_ff_2_q);
  or or_1 (or_1_out, and_1_out, Cout[1], Reset);
endmodule

module Time (
  output [3:0] H2,
  output [3:0] H1,
  output [3:0] M2,
  output [3:0] M1,
  output [3:0] S2,
  output [3:0] S1
);

  wire and_1_out, and_2_out, clock_1_out, not_1_out, not_2_out;
  wire [5:0] counter_1_q, counter_2_q, counter_3_q;

  Clock clock_1 (.out(clock_1_out));
  and and_1 (and_1_out, counter_1_q[0], counter_1_q[1], counter_1_q[3], counter_1_q[4], counter_1_q[5]);
  not not_1 (not_1_out, and_1_out);
  and and_2 (and_2_out, counter_2_q[0], counter_2_q[1], counter_2_q[3], counter_2_q[4], counter_2_q[5]);
  not not_2 (not_2_out, and_2_out);
  Counter #(.max('h3b), .width(6)) counter_1 (
    .clr(1'b0), .clk(clock_1_out), .Q(counter_1_q));  // open: load, up, count, D, carry
  Counter #(.max('h3b), .width(6)) counter_2 (
    .clr(1'b0), .clk(not_1_out), .Q(counter_2_q));  // open: load, up, count, D, carry
  Counter #(.max('h17), .width(6)) counter_3 (
    .clr(1'b0), .clk(not_2_out), .Q(counter_3_q));  // open: load, up, count, D, carry
  // Binary_to_BCD_converter #(.binvalue(6)) binary_to_bcd_converter_1: pin names not known; wires that end beside it: counter_3_q, H2, H1
  // Binary_to_BCD_converter #(.binvalue(6)) binary_to_bcd_converter_2: pin names not known; wires that end beside it: counter_1_q, S2, S1
  // Binary_to_BCD_converter #(.binvalue(6)) binary_to_bcd_converter_3: pin names not known; wires that end beside it: counter_2_q, M2, M1
endmodule

module ModernComputer (
  input  in_1,
  input  in_2,
  input  in_3,
  input  in_4,
  input  in_5,
  input  in_6,
  input  in_7,
  input  in_8,
  input  in_9,
  input  in_10,
  input  in_11,
  input  in_12,
  input  in_13,
  input  in_14,
  input  in_15,
  input  in_16,
  input  in_17,
  input  in_18,
  input  in_19,
  input  in_20,
  input  in_21,
  input  in_22,
  input  in_23,
  input  in_24,
  input  in_25,
  input  in_26,
  input  in_27,
  input  in_28,
  input  in_29,
  input  in_30,
  input  in_31,
  input  in_32,
  input  in_33,
  input  in_34,
  input  in_35,
  input  in_36,
  input  in_37,
  input  in_38,
  input  in_39,
  input  in_40,
  input  in_41,
  input  in_42,
  input  in_43,
  input  in_44,
  input  in_45,
  input  in_46,
  input  in_47,
  input  in_48,
  input  in_49,
  input  in_50,
  input  in_51,
  input  in_52,
  input  in_53,
  input  in_54
);

  wire and_2_out, and_3_out, and_4_out, and_5_out, and_6_out, and_7_out, and_8_out, and_9_out, and_10_out,
       and_11_out, and_12_out, and_13_out, and_14_out, and_15_out, and_16_out, and_17_out, and_18_out,
       and_19_out, and_20_out, and_21_out, and_22_out, and_23_out, and_24_out, and_25_out, and_26_out,
       and_27_out, and_28_out, and_29_out, and_30_out, and_31_out, and_32_out, and_33_out, button_1_out,
       button_2_out, button_3_out, button_4_out, button_5_out, button_6_out, button_7_out, button_8_out,
       button_9_out, button_10_out, button_11_out, button_12_out, button_13_out, button_14_out,
       button_15_out, button_16_out, button_17_out, decoder_1_out0, decoder_1_out1, decoder_2_out0,
       decoder_2_out1, decoder_3_out0, decoder_3_out1, decoder_4_out0, decoder_4_out1, decoder_4_out2,
       decoder_4_out3, decoder_5_out0, decoder_5_out1, decoder_5_out2, decoder_5_out3, decoder_6_out0,
       decoder_6_out1, decoder_6_out2, decoder_6_out3, decoder_7_out0, decoder_7_out1, decoder_7_out2,
       decoder_7_out3, decoder_8_out0, decoder_8_out1, decoder_8_out2, decoder_8_out3, decoder_9_out0,
       decoder_9_out1, decoder_9_out2, decoder_9_out3, decoder_10_out0, decoder_10_out1, decoder_11_out0,
       decoder_11_out1, decoder_12_out0, decoder_12_out1, decoder_13_out0, decoder_13_out1, decoder_14_out0,
       decoder_14_out1, decoder_14_out2, decoder_14_out3, decoder_15_out0, decoder_15_out1, decoder_15_out2,
       decoder_15_out3, decoder_16_out0, decoder_16_out1, decoder_16_out2, decoder_16_out3, decoder_17_out0,
       decoder_17_out1, decoder_17_out2, decoder_17_out3, decoder_18_out0, decoder_18_out1, decoder_18_out2,
       decoder_18_out3, decoder_19_out0, decoder_19_out1, decoder_19_out2, decoder_19_out3, decoder_20_out0,
       decoder_20_out1, decoder_20_out2, decoder_20_out3, decoder_21_out0, decoder_21_out1, decoder_21_out2,
       decoder_21_out3, decoder_22_out0, decoder_22_out1, decoder_22_out2, decoder_22_out3, decoder_23_out0,
       decoder_23_out1, decoder_23_out2, decoder_23_out3, decoder_24_out0, decoder_24_out1, decoder_24_out2,
       decoder_24_out3, decoder_25_out0, decoder_25_out1, decoder_25_out2, decoder_25_out3, decoder_26_out0,
       decoder_26_out1, decoder_27_out0, decoder_27_out1, decoder_28_out0, decoder_28_out1, decoder_28_out2,
       decoder_28_out3, decoder_29_out0, decoder_29_out1, decoder_29_out2, decoder_29_out3, decoder_30_out0,
       decoder_30_out1, decoder_30_out2, decoder_30_out3, decoder_31_out0, decoder_31_out1, decoder_31_out2,
       decoder_31_out3, decoder_32_out0, decoder_32_out1, decoder_32_out2, decoder_32_out3, decoder_33_out0,
       decoder_33_out1, decoder_33_out2, decoder_33_out3, fourbit2_1_vo, fourbit2_2_vo, fourbit2_3_vo,
       fourbit2_4_vo, fourbit2_5_vo, fourbit2_6_vo, fourbit2_7_vo, fourbit2_8_vo, LOAD_out, memcell_1_serout,
       memcell_2_serout, memcell_3_serout, memcell_4_serout, memcell_5_serout, memcell_6_serout,
       memcell_7_serout, memcell_8_serout, memcell_9_serout, memcell_10_serout, memcell_11_serout,
       memcell_12_serout, memcell_25_serout, memcell_26_serout, memcell_27_serout, memcell_28_serout,
       memcell_29_serout, memcell_30_serout, memcell_31_serout, memcell_32_serout, memcell_33_serout,
       memcell_34_serout, memcell_35_serout, memcell_36_serout, memcell_37_serout, memcell_38_serout,
       memcell_39_serout, memcell_40_serout, memcell_57_serout, memcell_58_serout, memcell_59_serout,
       memcell_60_serout, memcell_61_serout, memcell_62_serout, memcell_63_serout, memcell_64_serout,
       multiplexer_1_out, multiplexer_2_out, multiplexer_3_out, multiplexer_12_out, multiplexer_13_out,
       multiplexer_14_out, multiplexer_15_out, multiplexer_32_out, multiplexer_33_out, mydemux_1_d0,
       mydemux_1_d1, mydemux_1_d2, mydemux_1_d3, mydemux_2_d0, mydemux_2_d1, mydemux_2_d2, mydemux_2_d3,
       mydemux_3_d0, mydemux_3_d1, mydemux_3_d2, mydemux_3_d3, mydemux_4_d0, mydemux_4_d1, mydemux_4_d2,
       mydemux_4_d3, mydemux_5_d0, mydemux_5_d1, mydemux_5_d2, mydemux_5_d3, mydemux_6_d0, mydemux_6_d1,
       mydemux_6_d2, mydemux_6_d3, mydemux_7_d0, mydemux_7_d1, mydemux_7_d2, mydemux_7_d3, mydemux_8_d0,
       mydemux_8_d1, mydemux_8_d2, mydemux_8_d3, mydemux_9_d0, mydemux_9_d1, mydemux_9_d2, mydemux_9_d3,
       mydemux_10_d0, mydemux_10_d1, mydemux_10_d2, mydemux_10_d3, mydemux_11_d0, mydemux_11_d1,
       mydemux_11_d2, mydemux_11_d3, mydemux_12_d0, mydemux_12_d1, mydemux_12_d2, mydemux_12_d3,
       mydemux_13_d0, mydemux_13_d1, mydemux_13_d2, mydemux_13_d3, mydemux_14_d0, mydemux_14_d1,
       mydemux_14_d2, mydemux_14_d3, mydemux_15_d0, mydemux_15_d1, mydemux_15_d2, mydemux_15_d3,
       mydemux_16_d0, mydemux_16_d1, mydemux_16_d2, mydemux_16_d3, mydemux_17_d0, mydemux_17_d1,
       mydemux_17_d2, mydemux_17_d3, mydemux_18_d0, mydemux_18_d1, mydemux_18_d2, mydemux_18_d3,
       mydemux_19_d0, mydemux_19_d1, mydemux_19_d2, mydemux_19_d3, mydemux_20_d0, mydemux_20_d1,
       mydemux_20_d2, mydemux_20_d3, mydemux_21_d0, mydemux_21_d1, mydemux_21_d2, mydemux_21_d3,
       mydemux_22_d0, mydemux_22_d1, mydemux_22_d2, mydemux_22_d3, mydemux_23_d0, mydemux_23_d1,
       mydemux_23_d2, mydemux_23_d3, mydemux_24_d0, mydemux_24_d1, mydemux_24_d2, mydemux_24_d3,
       mydemux_25_d0, mydemux_25_d1, mydemux_25_d2, mydemux_25_d3, not_1_out, not_2_out, not_3_out,
       not_4_out, not_5_out, not_6_out, not_7_out, not_8_out, not_9_out, not_10_out, not_11_out, not_12_out,
       not_13_out, not_14_out, not_15_out, not_16_out, not_17_out, not_18_out, not_19_out, not_20_out,
       not_21_out, not_22_out, not_23_out, not_24_out, or_1_out, or_2_out, or_7_out, or_8_out, or_11_out,
       or_14_out, or_19_out, or_20_out, parser_1_do, parser_2_do, parser_3_do, parser_4_do, parser_5_do,
       parser_6_do, parser_7_do, parser_8_do, ReadingtoMem_d0, ReadingtoMem_d1, ReadingtoMem_d2,
       ReadingtoMem_d3, undriven_17, WritingToMem_d0, WritingToMem_d1, WritingToMem_d2, WritingToMem_d3;
  wire [1:0] fetcher_1_dout_2, fetcher_2_dout_2, fetcher_2_dout_3, fetcher_2_dout_4, fetcher_2_dout_5,
       PC_dout_2, PC_dout_3, PC_dout_4, PC_dout_5;
  wire [2:0] or_5_out, or_6_out, or_12_out, or_13_out, or_17_out, or_18_out, or_23_out, or_24_out;
  wire [3:0] fetcher_1_count, fetcher_2_count, fetcher_3_count, fetcher_4_count, fetcher_5_count,
       fetcher_6_count, fetcher_7_count, fetcher_8_count, fourbit2_1_r0, fourbit2_2_r0, fourbit2_3_r0,
       fourbit2_4_r0, fourbit2_5_r0, fourbit2_6_r0, fourbit2_7_r0, fourbit2_8_r0, memcell_1_parout,
       memcell_2_parout, memcell_3_parout, memcell_4_parout, memcell_5_parout, memcell_6_parout,
       memcell_7_parout, memcell_8_parout, memcell_9_parout, memcell_10_parout, memcell_11_parout,
       memcell_12_parout, memcell_13_parout, memcell_14_parout, memcell_15_parout, memcell_16_parout,
       memcell_17_parout, memcell_18_parout, memcell_19_parout, memcell_20_parout, memcell_25_parout,
       memcell_26_parout, memcell_27_parout, memcell_28_parout, memcell_29_parout, memcell_30_parout,
       memcell_31_parout, memcell_32_parout, memcell_33_parout, memcell_34_parout, memcell_35_parout,
       memcell_36_parout, memcell_37_parout, memcell_38_parout, memcell_39_parout, memcell_40_parout,
       memcell_41_parout, memcell_42_parout, memcell_43_parout, memcell_44_parout, memcell_45_parout,
       memcell_46_parout, memcell_47_parout, memcell_48_parout, memcell_49_parout, memcell_50_parout,
       memcell_51_parout, memcell_52_parout, memcell_53_parout, memcell_54_parout, memcell_55_parout,
       memcell_56_parout, memcell_57_parout, memcell_58_parout, memcell_59_parout, memcell_60_parout,
       memcell_61_parout, memcell_62_parout, memcell_63_parout, memcell_64_parout, memcell_65_parout,
       memcell_66_parout, memcell_67_parout, memcell_68_parout, memcell_69_parout, memcell_70_parout,
       memcell_71_parout, memcell_72_parout, multiplexer_4_out, multiplexer_5_out, multiplexer_6_out,
       multiplexer_7_out, multiplexer_8_out, multiplexer_9_out, multiplexer_10_out, multiplexer_11_out,
       multiplexer_16_out, multiplexer_17_out, multiplexer_18_out, multiplexer_19_out, multiplexer_20_out,
       multiplexer_21_out, multiplexer_22_out, multiplexer_23_out, multiplexer_24_out, multiplexer_25_out,
       multiplexer_26_out, multiplexer_27_out, multiplexer_28_out, multiplexer_29_out, multiplexer_30_out,
       multiplexer_31_out, multiplexer_34_out, multiplexer_35_out, multiplexer_36_out, multiplexer_37_out,
       multiplexer_38_out, multiplexer_39_out, multiplexer_40_out, multiplexer_41_out, PC_count;
  wire [11:0] fetcher_1_dout, fetcher_3_dout, fetcher_4_dout, fetcher_5_dout, fetcher_6_dout, fetcher_7_dout,
       fetcher_8_dout, undriven, undriven_2, undriven_3, undriven_4, undriven_5, undriven_6, undriven_7,
       undriven_8, undriven_9, undriven_10, undriven_11, undriven_12, undriven_13, undriven_14, undriven_15,
       undriven_16, undriven_18, undriven_19, undriven_20, undriven_21, undriven_22, undriven_23,
       undriven_24, undriven_25, undriven_26, undriven_27, undriven_28, undriven_29, undriven_30,
       undriven_31, undriven_32, undriven_33, undriven_34, undriven_35, undriven_36, undriven_37,
       undriven_38, undriven_39, undriven_40, undriven_41;
  wire [11:8] fetcher_2_dout, PC_dout;

  Button button_1 (.out(button_1_out));
  Button button_2 (.out(button_2_out));
  mydemux mydemux_1 (
    .Enable(1'b1), .C0(in_6), .C1(in_5), .Din(button_1_out), .D0(mydemux_1_d0), .D1(mydemux_1_d1),
    .D2(mydemux_1_d2), .D3(mydemux_1_d3));
  mydemux mydemux_2 (
    .Enable(1'b1), .C0(in_20), .C1(in_19), .Din(button_2_out), .D0(mydemux_2_d0), .D1(mydemux_2_d1),
    .D2(mydemux_2_d2), .D3(mydemux_2_d3));
  Button LOAD (.out(LOAD_out));
  Button button_3 (.out(button_3_out));
  Button button_4 (.out(button_4_out));
  mydemux mydemux_3 (
    .Enable(decoder_3_out0), .C0(fetcher_1_dout_2[0]), .C1(fetcher_1_dout_2[1]), .Din(1'b1),
    .D0(mydemux_3_d0), .D1(mydemux_3_d1), .D2(mydemux_3_d2), .D3(mydemux_3_d3));
  mydemux mydemux_4 (
    .Enable(decoder_3_out1), .C0(fetcher_1_dout_2[0]), .C1(fetcher_1_dout_2[1]), .Din(1'b1),
    .D0(mydemux_4_d0), .D1(mydemux_4_d1), .D2(mydemux_4_d2), .D3(mydemux_4_d3));
  mydemux mydemux_5 (
    .Enable(decoder_1_out0), .C0(fetcher_2_dout_2[0]), .C1(fetcher_2_dout_2[1]), .Din(1'b1),
    .D0(mydemux_5_d0), .D1(mydemux_5_d1), .D2(mydemux_5_d2), .D3(mydemux_5_d3));
  mydemux mydemux_6 (
    .Enable(decoder_1_out1), .C0(fetcher_2_dout_2[1]), .C1(fetcher_2_dout_2[0]), .Din(1'b1),
    .D0(mydemux_6_d0), .D1(mydemux_6_d1), .D2(mydemux_6_d2), .D3(mydemux_6_d3));
  Button button_5 (.out(button_5_out));
  mydemux ReadingtoMem (
    .Enable(decoder_2_out1), .C0(PC_dout_2[0]), .C1(PC_dout_2[1]), .Din(1'b1), .D0(ReadingtoMem_d0),
    .D1(ReadingtoMem_d1), .D2(ReadingtoMem_d2), .D3(ReadingtoMem_d3));
  mydemux WritingToMem (
    .Enable(decoder_2_out0), .C0(PC_dout_2[0]), .C1(PC_dout_2[1]), .Din(1'b1), .D0(WritingToMem_d0),
    .D1(WritingToMem_d1), .D2(WritingToMem_d2), .D3(WritingToMem_d3));
  Hex_Digit_Display hex_digit_display_1 (.value(fetcher_1_count));  // open: dp
  Hex_Digit_Display hex_digit_display_2 (.value(fetcher_2_count));  // open: dp
  mydemux mydemux_7 (
    .Enable(1'b1), .C0(in_48), .C1(in_47), .Din(LOAD_out), .D0(mydemux_7_d0), .D1(mydemux_7_d1),
    .D2(mydemux_7_d2), .D3(mydemux_7_d3));
  Hex_Digit_Display hex_digit_display_3 (.value(PC_count));  // open: dp
  Fetcher fetcher_1 (
    .RST(button_3_out), .num0(undriven_2), .num1(undriven), .num2(undriven_3), .num3(undriven_5),
    .num4(undriven_8), .num5(undriven_10), .num6(undriven_12), .num7(undriven_14), .count(fetcher_1_count),
    .Dout({fetcher_1_dout[11:6], fetcher_1_dout_2, fetcher_1_dout[3:0]}));  // open: N
  Fetcher fetcher_2 (
    .RST(button_4_out), .num0(undriven_6), .num1(undriven_4), .num2(undriven_7), .num3(undriven_9),
    .num4(undriven_11), .num5(undriven_13), .num6(undriven_15), .num7(undriven_16), .count(fetcher_2_count),
    .Dout({fetcher_2_dout, fetcher_2_dout_3, fetcher_2_dout_2, fetcher_2_dout_5, fetcher_2_dout_4}));  // open: N
  Decoder decoder_1 (.out0(decoder_1_out0), .out1(decoder_1_out1), .sel(fetcher_2_dout[10]), .en(fetcher_2_dout[11]));
  Fetcher PC (
    .RST(button_5_out), .num0(12'hc10), .num1(12'h240), .num2(12'h34a), .num3(12'h4c4), .count(PC_count),
    .Dout({PC_dout, PC_dout_3, PC_dout_2, PC_dout_5, PC_dout_4}));  // open: N, num4, num5, num6, num7
  Decoder decoder_2 (.out0(decoder_2_out0), .out1(decoder_2_out1), .sel(PC_dout[10]), .en(PC_dout[11]));
  Decoder decoder_3 (.out0(decoder_3_out0), .out1(decoder_3_out1), .sel(fetcher_1_dout[10]), .en(fetcher_1_dout[11]));
  Hex_Digit_Display hex_digit_display_4 (.value(memcell_5_parout));  // open: dp
  Hex_Digit_Display hex_digit_display_5 (.value(memcell_6_parout));  // open: dp
  Hex_Digit_Display hex_digit_display_6 (.value(memcell_7_parout));  // open: dp
  Hex_Digit_Display hex_digit_display_7 (.value(memcell_8_parout));  // open: dp
  // AND_Gate and_1 has open pins: in0=fetcher_1_dout[11], in1=fetcher_1_dout[10], out=open
  Hex_Digit_Display hex_digit_display_8 (.value(memcell_9_parout));  // open: dp
  Hex_Digit_Display hex_digit_display_9 (.value(memcell_10_parout));  // open: dp
  Hex_Digit_Display hex_digit_display_10 (.value(memcell_11_parout));  // open: dp
  Hex_Digit_Display hex_digit_display_11 (.value(memcell_12_parout));  // open: dp
  and and_2 (and_2_out, fetcher_2_dout_2[0], fetcher_2_dout_2[1]);
  Hex_Digit_Display hex_digit_display_12 (.value(memcell_1_parout));  // open: dp
  Hex_Digit_Display hex_digit_display_13 (.value(memcell_2_parout));  // open: dp
  Hex_Digit_Display hex_digit_display_14 (.value(memcell_3_parout));  // open: dp
  Hex_Digit_Display hex_digit_display_15 (.value(memcell_4_parout));  // open: dp
  and and_3 (and_3_out, PC_dout[11], PC_dout[10]);
  memcell memcell_1 (
    .Parlin({in_21, in_22, in_23, in_24}), .Load(mydemux_2_d0), .Serin(parser_1_do), .Read(mydemux_5_d0),
    .Write(mydemux_6_d0), .SerOut(memcell_1_serout), .ParOut(memcell_1_parout));
  memcell memcell_2 (
    .Parlin({in_21, in_22, in_23, in_24}), .Load(mydemux_2_d1), .Serin(parser_1_do), .Read(mydemux_5_d1),
    .Write(mydemux_6_d1), .SerOut(memcell_2_serout), .ParOut(memcell_2_parout));
  memcell memcell_3 (
    .Parlin({in_21, in_22, in_23, in_24}), .Load(mydemux_2_d2), .Serin(parser_1_do), .Read(mydemux_5_d2),
    .Write(mydemux_6_d2), .SerOut(memcell_3_serout), .ParOut(memcell_3_parout));
  memcell memcell_4 (
    .Parlin({in_21, in_22, in_23, in_24}), .Load(mydemux_2_d3), .Serin(parser_1_do), .Read(mydemux_5_d3),
    .Write(mydemux_6_d3), .SerOut(memcell_4_serout), .ParOut(memcell_4_parout));
  memcell memcell_5 (
    .Parlin({in_37, in_38, in_39, in_40}), .Load(mydemux_7_d0), .Serin(parser_2_do), .Read(ReadingtoMem_d0),
    .Write(WritingToMem_d0), .SerOut(memcell_5_serout), .ParOut(memcell_5_parout));
  memcell memcell_6 (
    .Parlin({in_37, in_38, in_39, in_40}), .Load(mydemux_7_d1), .Serin(parser_2_do), .Read(ReadingtoMem_d1),
    .Write(WritingToMem_d1), .SerOut(memcell_6_serout), .ParOut(memcell_6_parout));
  memcell memcell_7 (
    .Parlin({in_37, in_38, in_39, in_40}), .Load(mydemux_7_d2), .Serin(parser_2_do), .Read(ReadingtoMem_d2),
    .Write(WritingToMem_d2), .SerOut(memcell_7_serout), .ParOut(memcell_7_parout));
  memcell memcell_8 (
    .Parlin({in_37, in_38, in_39, in_40}), .Load(mydemux_7_d3), .Serin(parser_2_do), .Read(ReadingtoMem_d3),
    .Write(WritingToMem_d3), .SerOut(memcell_8_serout), .ParOut(memcell_8_parout));
  memcell memcell_9 (
    .Parlin({in_1, in_2, in_3, in_4}), .Load(mydemux_1_d0), .Serin(undriven_17), .Read(mydemux_3_d0),
    .Write(mydemux_4_d0), .SerOut(memcell_9_serout), .ParOut(memcell_9_parout));
  memcell memcell_10 (
    .Parlin({in_1, in_2, in_3, in_4}), .Load(mydemux_1_d1), .Serin(undriven_17), .Read(mydemux_3_d1),
    .Write(mydemux_4_d1), .SerOut(memcell_10_serout), .ParOut(memcell_10_parout));
  memcell memcell_11 (
    .Parlin({in_1, in_2, in_3, in_4}), .Load(mydemux_1_d2), .Serin(undriven_17), .Read(mydemux_3_d2),
    .Write(mydemux_4_d2), .SerOut(memcell_11_serout), .ParOut(memcell_11_parout));
  memcell memcell_12 (
    .Parlin({in_1, in_2, in_3, in_4}), .Load(mydemux_1_d3), .Serin(undriven_17), .Read(mydemux_3_d3),
    .Write(mydemux_4_d3), .SerOut(memcell_12_serout), .ParOut(memcell_12_parout));
  Clock clock_1 ();  // open: out
  Multiplexer #(.select(2)) multiplexer_1 (
    .in0(memcell_5_serout), .in1(memcell_6_serout), .in2(memcell_7_serout), .in3(memcell_8_serout),
    .out(multiplexer_1_out), .sel(PC_dout_2));
  Multiplexer #(.select(2)) multiplexer_2 (
    .in0(memcell_1_serout), .in1(memcell_2_serout), .in2(memcell_3_serout), .in3(memcell_4_serout),
    .out(multiplexer_2_out), .sel(fetcher_2_dout_2));
  Multiplexer #(.select(2)) multiplexer_3 (
    .in0(memcell_9_serout), .in1(memcell_10_serout), .in2(memcell_11_serout), .in3(memcell_12_serout),
    .out(multiplexer_3_out), .sel(fetcher_1_dout_2));
  parser parser_1 (.Din(multiplexer_5_out), .Do(parser_1_do));
  parser parser_2 (.Din(multiplexer_7_out), .Do(parser_2_do));
  not not_1 (not_1_out, PC_dout[11]);
  and and_4 (and_4_out, not_1_out, PC_dout[10]);
  or or_1 (or_1_out, PC_dout[9], and_4_out);
  Decoder #(.select(2)) decoder_4 (
    .out0(decoder_4_out0), .out1(decoder_4_out1), .out2(decoder_4_out2), .out3(decoder_4_out3),
    .sel(PC_dout_3), .en(or_1_out));
  not not_2 (not_2_out, fetcher_2_dout_2[0]);
  and and_5 (and_5_out, not_2_out, fetcher_2_dout[10]);
  or or_2 (or_2_out, fetcher_2_dout[9], and_5_out);
  Decoder #(.select(2)) decoder_5 (
    .out0(decoder_5_out0), .out1(decoder_5_out1), .out2(decoder_5_out2), .out3(decoder_5_out3),
    .sel(fetcher_2_dout_3), .en(or_2_out));
  not not_3 (not_3_out, PC_dout[10]);
  and and_6 (and_6_out, PC_dout[11], not_3_out);
  Decoder #(.select(2)) decoder_6 (
    .out0(decoder_6_out0), .out1(decoder_6_out1), .out2(decoder_6_out2), .out3(decoder_6_out3),
    .sel(PC_dout_2), .en(and_6_out));
  not not_4 (not_4_out, fetcher_2_dout[10]);
  and and_7 (and_7_out, fetcher_2_dout_2[0], not_4_out);
  Decoder #(.select(2)) decoder_7 (
    .out0(decoder_7_out0), .out1(decoder_7_out1), .out2(decoder_7_out2), .out3(decoder_7_out3),
    .sel(fetcher_2_dout_2), .en(and_7_out));
  Decoder #(.select(2)) decoder_8 (
    .out0(decoder_8_out0), .out1(decoder_8_out1), .out2(decoder_8_out2), .out3(decoder_8_out3),
    .sel(fetcher_2_dout_3), .en(and_2_out));
  LED led_1 (.in(fourbit2_1_r0[0]));
  LED led_2 (.in(fourbit2_1_r0[1]));
  LED led_3 (.in(fourbit2_1_r0[2]));
  LED led_4 (.in(fourbit2_1_r0[3]));
  Decoder #(.select(2)) decoder_9 (
    .out0(decoder_9_out0), .out1(decoder_9_out1), .out2(decoder_9_out2), .out3(decoder_9_out3),
    .sel(PC_dout_3), .en(and_3_out));
  Multiplexer #(.select(3), .width(4)) multiplexer_4 (
    .in0(memcell_13_parout), .in1(memcell_14_parout), .in2(memcell_15_parout), .in3(memcell_16_parout),
    .in4({PC_dout_5, PC_dout_4}), .out(multiplexer_4_out), .sel({1'b0, PC_dout_2}));  // open: in5, in6, in7
  LED led_5 (.in(fourbit2_2_r0[0]));
  LED led_6 (.in(fourbit2_2_r0[1]));
  LED led_7 (.in(fourbit2_2_r0[2]));
  LED led_8 (.in(fourbit2_2_r0[3]));
  and and_8 (and_8_out, fetcher_2_dout[10], not_5_out);
  not not_5 (not_5_out, fetcher_2_dout[11]);
  Multiplexer #(.select(3), .width(4)) multiplexer_5 (
    .in0(memcell_17_parout), .in1(memcell_18_parout), .in2(memcell_19_parout), .in3(memcell_20_parout),
    .in4(fourbit2_1_r0), .out(multiplexer_5_out));  // open: in5, in6, in7, sel
  LED led_9 (.in(fourbit2_1_vo));
  fourbit2 fourbit2_1 (
    .Ain(multiplexer_9_out), .Bin(multiplexer_8_out), .Vo(fourbit2_1_vo), .R3(fourbit2_1_r0[3]),
    .R2(fourbit2_1_r0[2]), .R1(fourbit2_1_r0[1]), .R0(fourbit2_1_r0[0]));
  and and_9 (and_9_out, PC_dout[10], not_6_out);
  not not_6 (not_6_out, PC_dout[11]);
  Multiplexer #(.select(3), .width(4)) multiplexer_6 (
    .in0(memcell_13_parout), .in1(memcell_14_parout), .in2(memcell_15_parout), .in3(memcell_16_parout),
    .in4({PC_dout_5, PC_dout_4}), .out(multiplexer_6_out), .sel({1'b0, PC_dout_5}));  // open: in5, in6, in7
  Multiplexer #(.select(3), .width(4)) multiplexer_7 (
    .in0(memcell_13_parout), .in1(memcell_14_parout), .in2(memcell_15_parout), .in3(memcell_16_parout),
    .in4(fourbit2_2_r0), .out(multiplexer_7_out));  // open: in5, in6, in7, sel
  LED led_10 (.in(fourbit2_2_vo));
  fourbit2 fourbit2_2 (
    .Ain(multiplexer_6_out), .Bin(multiplexer_4_out), .Vo(fourbit2_2_vo), .R3(fourbit2_2_r0[3]),
    .R2(fourbit2_2_r0[2]), .R1(fourbit2_2_r0[1]), .R0(fourbit2_2_r0[0]));
  or or_3 (or_5_out[2], and_8_out, fetcher_2_dout[8]);
  Multiplexer #(.select(3), .width(4)) multiplexer_8 (
    .in0(memcell_17_parout), .in1(memcell_18_parout), .in2(memcell_19_parout), .in3(memcell_20_parout),
    .in4({fetcher_2_dout_5, fetcher_2_dout_4}), .out(multiplexer_8_out), .sel({1'b0, fetcher_2_dout_2}));  // open: in5, in6, in7
  Multiplexer #(.select(3), .width(4)) multiplexer_9 (
    .in0(memcell_17_parout), .in1(memcell_18_parout), .in2(memcell_19_parout), .in3(memcell_20_parout),
    .in4({fetcher_2_dout_5, fetcher_2_dout_4}), .out(multiplexer_9_out), .sel({1'b0, fetcher_2_dout_5}));  // open: in5, in6, in7
  or or_4 (or_6_out[2], and_9_out, PC_dout[8]);
  or or_5 (or_5_out[0], and_8_out, fetcher_2_dout_2[0]);
  or or_6 (or_6_out[0], and_9_out, PC_dout_2[0]);
  Hex_Digit_Display hex_digit_display_16 (.value(memcell_13_parout));  // open: dp
  Hex_Digit_Display hex_digit_display_17 (.value(memcell_14_parout));  // open: dp
  Hex_Digit_Display hex_digit_display_18 (.value(memcell_15_parout));  // open: dp
  Hex_Digit_Display hex_digit_display_19 (.value(memcell_16_parout));  // open: dp
  Multiplexer #(.select(3), .width(4)) multiplexer_10 (
    .in0(memcell_17_parout), .in1(memcell_18_parout), .in2(memcell_19_parout), .in3(memcell_20_parout),
    .in4({fetcher_2_dout_5, fetcher_2_dout_4}), .in5(fourbit2_1_r0), .out(multiplexer_10_out),
    .sel({or_5_out[2], fetcher_2_dout_2[1], or_5_out[0]}));  // open: in6, in7
  Hex_Digit_Display hex_digit_display_20 (.value(memcell_17_parout));  // open: dp
  Hex_Digit_Display hex_digit_display_21 (.value(memcell_18_parout));  // open: dp
  Hex_Digit_Display hex_digit_display_22 (.value(memcell_19_parout));  // open: dp
  Hex_Digit_Display hex_digit_display_23 (.value(memcell_20_parout));  // open: dp
  Multiplexer #(.select(3), .width(4)) multiplexer_11 (
    .in0(memcell_13_parout), .in1(memcell_14_parout), .in2(memcell_15_parout), .in3(memcell_16_parout),
    .in4({PC_dout_5, PC_dout_4}), .in5(fourbit2_2_r0), .out(multiplexer_11_out),
    .sel({or_6_out[2], PC_dout_2[1], or_6_out[0]}));  // open: in6, in7
  memcell memcell_13 (
    .Parlin(multiplexer_11_out), .Load(decoder_4_out0), .Serin(multiplexer_1_out), .Read(decoder_6_out0),
    .Write(decoder_9_out0), .ParOut(memcell_13_parout));  // open: SerOut
  memcell memcell_14 (
    .Parlin(multiplexer_11_out), .Load(decoder_4_out1), .Serin(multiplexer_1_out), .Read(decoder_6_out1),
    .Write(decoder_9_out1), .ParOut(memcell_14_parout));  // open: SerOut
  memcell memcell_15 (
    .Parlin(multiplexer_11_out), .Load(decoder_4_out2), .Serin(multiplexer_1_out), .Read(decoder_6_out2),
    .Write(decoder_9_out2), .ParOut(memcell_15_parout));  // open: SerOut
  memcell memcell_16 (
    .Parlin(multiplexer_11_out), .Load(decoder_4_out3), .Serin(multiplexer_1_out), .Read(decoder_6_out3),
    .Write(decoder_9_out3), .ParOut(memcell_16_parout));  // open: SerOut
  memcell memcell_17 (
    .Parlin(multiplexer_10_out), .Load(decoder_5_out0), .Serin(multiplexer_2_out), .Read(decoder_7_out0),
    .Write(decoder_8_out0), .ParOut(memcell_17_parout));  // open: SerOut
  memcell memcell_18 (
    .Parlin(multiplexer_10_out), .Load(decoder_5_out1), .Serin(multiplexer_2_out), .Read(decoder_7_out1),
    .Write(decoder_8_out1), .ParOut(memcell_18_parout));  // open: SerOut
  memcell memcell_19 (
    .Parlin(multiplexer_10_out), .Load(decoder_5_out2), .Serin(multiplexer_2_out), .Read(decoder_7_out2),
    .Write(decoder_8_out2), .ParOut(memcell_19_parout));  // open: SerOut
  memcell memcell_20 (
    .Parlin(multiplexer_10_out), .Load(decoder_5_out3), .Serin(multiplexer_2_out), .Read(decoder_7_out3),
    .Write(decoder_8_out3), .ParOut(memcell_20_parout));  // open: SerOut
  memcell memcell_21 (.Serin(multiplexer_3_out));  // open: Parlin, Load, Read, Write, SerOut, ParOut
  memcell memcell_22 (.Serin(multiplexer_3_out));  // open: Parlin, Load, Read, Write, SerOut, ParOut
  memcell memcell_23 (.Serin(multiplexer_3_out));  // open: Parlin, Load, Read, Write, SerOut, ParOut
  memcell memcell_24 (.Serin(multiplexer_3_out));  // open: Parlin, Load, Read, Write, SerOut, ParOut
  Button button_6 (.out(button_6_out));
  mydemux mydemux_8 (
    .Enable(1'b1), .C0(in_8), .C1(in_7), .Din(button_6_out), .D0(mydemux_8_d0), .D1(mydemux_8_d1),
    .D2(mydemux_8_d2), .D3(mydemux_8_d3));
  Button button_7 (.out(button_7_out));
  Button button_8 (.out(button_8_out));
  mydemux mydemux_9 (
    .Enable(decoder_11_out1), .C0(fetcher_4_dout[4]), .C1(fetcher_4_dout[5]), .Din(1'b1), .D0(mydemux_9_d0),
    .D1(mydemux_9_d1), .D2(mydemux_9_d2), .D3(mydemux_9_d3));
  mydemux mydemux_10 (
    .Enable(decoder_11_out0), .C0(fetcher_4_dout[4]), .C1(fetcher_4_dout[5]), .Din(1'b1), .D0(mydemux_10_d0),
    .D1(mydemux_10_d1), .D2(mydemux_10_d2), .D3(mydemux_10_d3));
  mydemux mydemux_11 (
    .Enable(decoder_10_out0), .C0(fetcher_3_dout[4]), .C1(fetcher_3_dout[5]), .Din(1'b1), .D0(mydemux_11_d0),
    .D1(mydemux_11_d1), .D2(mydemux_11_d2), .D3(mydemux_11_d3));
  mydemux mydemux_12 (
    .Enable(decoder_10_out1), .C0(fetcher_3_dout[5]), .C1(fetcher_3_dout[4]), .Din(1'b1), .D0(mydemux_12_d0),
    .D1(mydemux_12_d1), .D2(mydemux_12_d2), .D3(mydemux_12_d3));
  Button button_9 (.out(button_9_out));
  mydemux mydemux_13 (
    .Enable(1'b1), .C0(in_34), .C1(in_33), .Din(button_7_out), .D0(mydemux_13_d0), .D1(mydemux_13_d1),
    .D2(mydemux_13_d2), .D3(mydemux_13_d3));
  Hex_Digit_Display hex_digit_display_24 (.value(fetcher_3_count));  // open: dp
  Hex_Digit_Display hex_digit_display_25 (.value(fetcher_4_count));  // open: dp
  Button button_10 (.out(button_10_out));
  Fetcher fetcher_3 (
    .RST(button_8_out), .num0(undriven_19), .num1(undriven_18), .num2(undriven_20), .num3(undriven_21),
    .num4(undriven_22), .num5(undriven_23), .num6(undriven_24), .num7(undriven_25), .count(fetcher_3_count),
    .Dout(fetcher_3_dout));  // open: N
  mydemux mydemux_14 (
    .Enable(1'b1), .C0(in_42), .C1(in_41), .Din(button_10_out), .D0(mydemux_14_d0), .D1(mydemux_14_d1),
    .D2(mydemux_14_d2), .D3(mydemux_14_d3));
  Decoder decoder_10 (
    .out0(decoder_10_out0), .out1(decoder_10_out1), .sel(fetcher_3_dout[10]), .en(fetcher_3_dout[11]));
  Fetcher fetcher_4 (
    .RST(button_9_out), .num0(12'hc10), .num1(12'h240), .num2(12'h34a), .num3(12'h4c4),
    .count(fetcher_4_count), .Dout(fetcher_4_dout));  // open: N, num4, num5, num6, num7
  Decoder decoder_11 (
    .out0(decoder_11_out0), .out1(decoder_11_out1), .sel(fetcher_4_dout[10]), .en(fetcher_4_dout[11]));
  Button button_11 (.out(button_11_out));
  Button button_12 (.out(button_12_out));
  and and_10 (and_10_out, fetcher_3_dout[4], fetcher_3_dout[5]);
  Hex_Digit_Display hex_digit_display_26 (.value(memcell_25_parout));  // open: dp
  Hex_Digit_Display hex_digit_display_27 (.value(memcell_26_parout));  // open: dp
  Hex_Digit_Display hex_digit_display_28 (.value(memcell_27_parout));  // open: dp
  Hex_Digit_Display hex_digit_display_29 (.value(memcell_28_parout));  // open: dp
  and and_11 (and_11_out, fetcher_4_dout[11], fetcher_4_dout[10]);
  Hex_Digit_Display hex_digit_display_30 (.value(memcell_29_parout));  // open: dp
  Hex_Digit_Display hex_digit_display_31 (.value(memcell_30_parout));  // open: dp
  Hex_Digit_Display hex_digit_display_32 (.value(memcell_31_parout));  // open: dp
  Hex_Digit_Display hex_digit_display_33 (.value(memcell_32_parout));  // open: dp
  mydemux mydemux_15 (
    .Enable(decoder_13_out1), .C0(fetcher_6_dout[4]), .C1(fetcher_6_dout[5]), .Din(1'b1), .D0(mydemux_15_d0),
    .D1(mydemux_15_d1), .D2(mydemux_15_d2), .D3(mydemux_15_d3));
  mydemux mydemux_16 (
    .Enable(decoder_13_out0), .C0(fetcher_6_dout[4]), .C1(fetcher_6_dout[5]), .Din(1'b1), .D0(mydemux_16_d0),
    .D1(mydemux_16_d1), .D2(mydemux_16_d2), .D3(mydemux_16_d3));
  mydemux mydemux_17 (
    .Enable(decoder_12_out0), .C0(fetcher_5_dout[4]), .C1(fetcher_5_dout[5]), .Din(1'b1), .D0(mydemux_17_d0),
    .D1(mydemux_17_d1), .D2(mydemux_17_d2), .D3(mydemux_17_d3));
  mydemux mydemux_18 (
    .Enable(decoder_12_out1), .C0(fetcher_5_dout[5]), .C1(fetcher_5_dout[4]), .Din(1'b1), .D0(mydemux_18_d0),
    .D1(mydemux_18_d1), .D2(mydemux_18_d2), .D3(mydemux_18_d3));
  Button button_13 (.out(button_13_out));
  mydemux mydemux_19 (
    .Enable(1'b1), .C0(in_54), .C1(in_53), .Din(button_11_out), .D0(mydemux_19_d0), .D1(mydemux_19_d1),
    .D2(mydemux_19_d2), .D3(mydemux_19_d3));
  memcell memcell_25 (
    .Parlin({in_9, in_10, in_11, in_12}), .Load(mydemux_8_d0), .Serin(parser_4_do), .Read(mydemux_11_d0),
    .Write(mydemux_12_d0), .SerOut(memcell_25_serout), .ParOut(memcell_25_parout));
  memcell memcell_26 (
    .Parlin({in_9, in_10, in_11, in_12}), .Load(mydemux_8_d1), .Serin(parser_4_do), .Read(mydemux_11_d1),
    .Write(mydemux_12_d1), .SerOut(memcell_26_serout), .ParOut(memcell_26_parout));
  memcell memcell_27 (
    .Parlin({in_9, in_10, in_11, in_12}), .Load(mydemux_8_d2), .Serin(parser_4_do), .Read(mydemux_11_d2),
    .Write(mydemux_12_d2), .SerOut(memcell_27_serout), .ParOut(memcell_27_parout));
  memcell memcell_28 (
    .Parlin({in_9, in_10, in_11, in_12}), .Load(mydemux_8_d3), .Serin(parser_4_do), .Read(mydemux_11_d3),
    .Write(mydemux_12_d3), .SerOut(memcell_28_serout), .ParOut(memcell_28_parout));
  Clock clock_2 ();  // open: out
  memcell memcell_29 (
    .Parlin({in_25, in_26, in_27, in_28}), .Load(mydemux_13_d0), .Serin(parser_3_do), .Read(mydemux_9_d0),
    .Write(mydemux_10_d0), .SerOut(memcell_29_serout), .ParOut(memcell_29_parout));
  memcell memcell_30 (
    .Parlin({in_25, in_26, in_27, in_28}), .Load(mydemux_13_d1), .Serin(parser_3_do), .Read(mydemux_9_d1),
    .Write(mydemux_10_d1), .SerOut(memcell_30_serout), .ParOut(memcell_30_parout));
  memcell memcell_31 (
    .Parlin({in_25, in_26, in_27, in_28}), .Load(mydemux_13_d2), .Serin(parser_3_do), .Read(mydemux_9_d2),
    .Write(mydemux_10_d2), .SerOut(memcell_31_serout), .ParOut(memcell_31_parout));
  memcell memcell_32 (
    .Parlin({in_25, in_26, in_27, in_28}), .Load(mydemux_13_d3), .Serin(parser_3_do), .Read(mydemux_9_d3),
    .Write(mydemux_10_d3), .SerOut(memcell_32_serout), .ParOut(memcell_32_parout));
  Hex_Digit_Display hex_digit_display_34 (.value(fetcher_5_count));  // open: dp
  Hex_Digit_Display hex_digit_display_35 (.value(fetcher_6_count));  // open: dp
  Fetcher fetcher_5 (
    .RST(button_12_out), .num0(undriven_27), .num1(undriven_26), .num2(undriven_28), .num3(undriven_29),
    .num4(undriven_30), .num5(undriven_31), .num6(undriven_32), .num7(undriven_33), .count(fetcher_5_count),
    .Dout(fetcher_5_dout));  // open: N
  Decoder decoder_12 (
    .out0(decoder_12_out0), .out1(decoder_12_out1), .sel(fetcher_5_dout[10]), .en(fetcher_5_dout[11]));
  Fetcher fetcher_6 (
    .RST(button_13_out), .num0(12'hc10), .num1(12'h240), .num2(12'h34a), .num3(12'h4c4),
    .count(fetcher_6_count), .Dout(fetcher_6_dout));  // open: N, num4, num5, num6, num7
  Decoder decoder_13 (
    .out0(decoder_13_out0), .out1(decoder_13_out1), .sel(fetcher_6_dout[10]), .en(fetcher_6_dout[11]));
  Multiplexer #(.select(2)) multiplexer_12 (
    .in0(memcell_25_serout), .in1(memcell_26_serout), .in2(memcell_27_serout), .in3(memcell_28_serout),
    .out(multiplexer_12_out), .sel(fetcher_3_dout[5:4]));
  Multiplexer #(.select(2)) multiplexer_13 (
    .in0(memcell_29_serout), .in1(memcell_30_serout), .in2(memcell_31_serout), .in3(memcell_32_serout),
    .out(multiplexer_13_out), .sel(fetcher_4_dout[5:4]));
  and and_12 (and_12_out, fetcher_5_dout[4], fetcher_5_dout[5]);
  Hex_Digit_Display hex_digit_display_36 (.value(memcell_33_parout));  // open: dp
  Hex_Digit_Display hex_digit_display_37 (.value(memcell_34_parout));  // open: dp
  Hex_Digit_Display hex_digit_display_38 (.value(memcell_35_parout));  // open: dp
  Hex_Digit_Display hex_digit_display_39 (.value(memcell_36_parout));  // open: dp
  and and_13 (and_13_out, fetcher_6_dout[11], fetcher_6_dout[10]);
  Hex_Digit_Display hex_digit_display_40 (.value(memcell_37_parout));  // open: dp
  Hex_Digit_Display hex_digit_display_41 (.value(memcell_38_parout));  // open: dp
  Hex_Digit_Display hex_digit_display_42 (.value(memcell_39_parout));  // open: dp
  Hex_Digit_Display hex_digit_display_43 (.value(memcell_40_parout));  // open: dp
  parser parser_3 (.Din(multiplexer_21_out), .Do(parser_3_do));
  parser parser_4 (.Din(multiplexer_19_out), .Do(parser_4_do));
  not not_7 (not_7_out, fetcher_4_dout[11]);
  and and_14 (and_14_out, not_7_out, fetcher_4_dout[10]);
  or or_7 (or_7_out, fetcher_4_dout[9], and_14_out);
  memcell memcell_33 (
    .Parlin({in_43, in_44, in_45, in_46}), .Load(mydemux_14_d0), .Serin(parser_6_do), .Read(mydemux_17_d0),
    .Write(mydemux_18_d0), .SerOut(memcell_33_serout), .ParOut(memcell_33_parout));
  memcell memcell_34 (
    .Parlin({in_43, in_44, in_45, in_46}), .Load(mydemux_14_d1), .Serin(parser_6_do), .Read(mydemux_17_d1),
    .Write(mydemux_18_d1), .SerOut(memcell_34_serout), .ParOut(memcell_34_parout));
  memcell memcell_35 (
    .Parlin({in_43, in_44, in_45, in_46}), .Load(mydemux_14_d2), .Serin(parser_6_do), .Read(mydemux_17_d2),
    .Write(mydemux_18_d2), .SerOut(memcell_35_serout), .ParOut(memcell_35_parout));
  memcell memcell_36 (
    .Parlin({in_43, in_44, in_45, in_46}), .Load(mydemux_14_d3), .Serin(parser_6_do), .Read(mydemux_17_d3),
    .Write(mydemux_18_d3), .SerOut(memcell_36_serout), .ParOut(memcell_36_parout));
  Clock clock_3 ();  // open: out
  memcell memcell_37 (
    .Parlin({in_49, in_50, in_51, in_52}), .Load(mydemux_19_d0), .Serin(parser_5_do), .Read(mydemux_15_d0),
    .Write(mydemux_16_d0), .SerOut(memcell_37_serout), .ParOut(memcell_37_parout));
  memcell memcell_38 (
    .Parlin({in_49, in_50, in_51, in_52}), .Load(mydemux_19_d1), .Serin(parser_5_do), .Read(mydemux_15_d1),
    .Write(mydemux_16_d1), .SerOut(memcell_38_serout), .ParOut(memcell_38_parout));
  memcell memcell_39 (
    .Parlin({in_49, in_50, in_51, in_52}), .Load(mydemux_19_d2), .Serin(parser_5_do), .Read(mydemux_15_d2),
    .Write(mydemux_16_d2), .SerOut(memcell_39_serout), .ParOut(memcell_39_parout));
  memcell memcell_40 (
    .Parlin({in_49, in_50, in_51, in_52}), .Load(mydemux_19_d3), .Serin(parser_5_do), .Read(mydemux_15_d3),
    .Write(mydemux_16_d3), .SerOut(memcell_40_serout), .ParOut(memcell_40_parout));
  Decoder #(.select(2)) decoder_14 (
    .out0(decoder_14_out0), .out1(decoder_14_out1), .out2(decoder_14_out2), .out3(decoder_14_out3),
    .sel(fetcher_4_dout[7:6]), .en(or_7_out));
  not not_8 (not_8_out, fetcher_3_dout[4]);
  and and_15 (and_15_out, not_8_out, fetcher_3_dout[10]);
  or or_8 (or_8_out, fetcher_3_dout[9], and_15_out);
  Decoder #(.select(2)) decoder_15 (
    .out0(decoder_15_out0), .out1(decoder_15_out1), .out2(decoder_15_out2), .out3(decoder_15_out3),
    .sel(fetcher_3_dout[7:6]), .en(or_8_out));
  not not_9 (not_9_out, fetcher_4_dout[10]);
  and and_16 (and_16_out, fetcher_4_dout[11], not_9_out);
  Decoder #(.select(2)) decoder_16 (
    .out0(decoder_16_out0), .out1(decoder_16_out1), .out2(decoder_16_out2), .out3(decoder_16_out3),
    .sel(fetcher_4_dout[5:4]), .en(and_16_out));
  not not_10 (not_10_out, fetcher_3_dout[10]);
  and and_17 (and_17_out, fetcher_3_dout[4], not_10_out);
  Decoder #(.select(2)) decoder_17 (
    .out0(decoder_17_out0), .out1(decoder_17_out1), .out2(decoder_17_out2), .out3(decoder_17_out3),
    .sel(fetcher_3_dout[5:4]), .en(and_17_out));
  LED led_11 (.in(fourbit2_3_r0[0]));
  Decoder #(.select(2)) decoder_18 (
    .out0(decoder_18_out0), .out1(decoder_18_out1), .out2(decoder_18_out2), .out3(decoder_18_out3),
    .sel(fetcher_4_dout[7:6]), .en(and_11_out));
  LED led_12 (.in(fourbit2_4_r0[0]));
  LED led_13 (.in(fourbit2_4_r0[1]));
  Multiplexer #(.select(2)) multiplexer_14 (
    .in0(memcell_33_serout), .in1(memcell_34_serout), .in2(memcell_35_serout), .in3(memcell_36_serout),
    .out(multiplexer_14_out), .sel(fetcher_5_dout[5:4]));
  Multiplexer #(.select(2)) multiplexer_15 (
    .in0(memcell_37_serout), .in1(memcell_38_serout), .in2(memcell_39_serout), .in3(memcell_40_serout),
    .out(multiplexer_15_out), .sel(fetcher_6_dout[5:4]));
  Decoder #(.select(2)) decoder_19 (
    .out0(decoder_19_out0), .out1(decoder_19_out1), .out2(decoder_19_out2), .out3(decoder_19_out3),
    .sel(fetcher_3_dout[7:6]), .en(and_10_out));
  fourbit2 fourbit2_3 (
    .Ain(multiplexer_18_out), .Bin(multiplexer_17_out), .Vo(fourbit2_3_vo), .R3(fourbit2_3_r0[3]),
    .R2(fourbit2_3_r0[2]), .R1(fourbit2_3_r0[1]), .R0(fourbit2_3_r0[0]));
  LED led_14 (.in(fourbit2_3_r0[1]));
  LED led_15 (.in(fourbit2_3_r0[2]));
  LED led_16 (.in(fourbit2_3_r0[3]));
  Multiplexer #(.select(3), .width(4)) multiplexer_16 (
    .in0(memcell_41_parout), .in1(memcell_42_parout), .in2(memcell_43_parout), .in3(memcell_44_parout),
    .in4(fetcher_4_dout[3:0]), .out(multiplexer_16_out), .sel({1'b0, fetcher_4_dout[5:4]}));  // open: in5, in6, in7
  LED led_17 (.in(fourbit2_4_vo));
  fourbit2 fourbit2_4 (
    .Ain(multiplexer_20_out), .Bin(multiplexer_16_out), .Vo(fourbit2_4_vo), .R3(fourbit2_4_r0[3]),
    .R2(fourbit2_4_r0[2]), .R1(fourbit2_4_r0[1]), .R0(fourbit2_4_r0[0]));
  LED led_18 (.in(fourbit2_4_r0[2]));
  LED led_19 (.in(fourbit2_4_r0[3]));
  and and_18 (and_18_out, fetcher_3_dout[10], not_11_out);
  not not_11 (not_11_out, fetcher_3_dout[11]);
  Multiplexer #(.select(3), .width(4)) multiplexer_17 (
    .in0(memcell_45_parout), .in1(memcell_46_parout), .in2(memcell_47_parout), .in3(memcell_48_parout),
    .in4(fetcher_3_dout[3:0]), .out(multiplexer_17_out), .sel({1'b0, fetcher_3_dout[5:4]}));  // open: in5, in6, in7
  Multiplexer #(.select(3), .width(4)) multiplexer_18 (
    .in0(memcell_45_parout), .in1(memcell_46_parout), .in2(memcell_47_parout), .in3(memcell_48_parout),
    .in4(fetcher_3_dout[3:0]), .out(multiplexer_18_out), .sel({1'b0, fetcher_3_dout[3:2]}));  // open: in5, in6, in7
  Multiplexer #(.select(3), .width(4)) multiplexer_19 (
    .in0(memcell_45_parout), .in1(memcell_46_parout), .in2(memcell_47_parout), .in3(memcell_48_parout),
    .in4(fourbit2_3_r0), .out(multiplexer_19_out));  // open: in5, in6, in7, sel
  LED led_20 (.in(fourbit2_3_vo));
  and and_19 (and_19_out, fetcher_4_dout[10], not_12_out);
  not not_12 (not_12_out, fetcher_4_dout[11]);
  or or_9 (or_13_out[2], and_19_out, fetcher_4_dout[8]);
  Multiplexer #(.select(3), .width(4)) multiplexer_20 (
    .in0(memcell_41_parout), .in1(memcell_42_parout), .in2(memcell_43_parout), .in3(memcell_44_parout),
    .in4(fetcher_4_dout[3:0]), .out(multiplexer_20_out), .sel({1'b0, fetcher_4_dout[3:2]}));  // open: in5, in6, in7
  Multiplexer #(.select(3), .width(4)) multiplexer_21 (
    .in0(memcell_41_parout), .in1(memcell_42_parout), .in2(memcell_43_parout), .in3(memcell_44_parout),
    .in4(fourbit2_4_r0), .out(multiplexer_21_out));  // open: in5, in6, in7, sel
  parser parser_5 (.Din(multiplexer_29_out), .Do(parser_5_do));
  or or_10 (or_12_out[2], and_18_out, fetcher_3_dout[8]);
  Hex_Digit_Display hex_digit_display_44 (.value(memcell_41_parout));  // open: dp
  Hex_Digit_Display hex_digit_display_45 (.value(memcell_42_parout));  // open: dp
  Hex_Digit_Display hex_digit_display_46 (.value(memcell_43_parout));  // open: dp
  Hex_Digit_Display hex_digit_display_47 (.value(memcell_44_parout));  // open: dp
  parser parser_6 (.Din(multiplexer_27_out), .Do(parser_6_do));
  not not_13 (not_13_out, fetcher_6_dout[11]);
  and and_20 (and_20_out, not_13_out, fetcher_6_dout[10]);
  or or_11 (or_11_out, fetcher_6_dout[9], and_20_out);
  or or_12 (or_12_out[0], and_18_out, fetcher_3_dout[4]);
  Hex_Digit_Display hex_digit_display_48 (.value(memcell_45_parout));  // open: dp
  Hex_Digit_Display hex_digit_display_49 (.value(memcell_46_parout));  // open: dp
  Hex_Digit_Display hex_digit_display_50 (.value(memcell_47_parout));  // open: dp
  Hex_Digit_Display hex_digit_display_51 (.value(memcell_48_parout));  // open: dp
  or or_13 (or_13_out[0], and_19_out, fetcher_4_dout[4]);
  Multiplexer #(.select(3), .width(4)) multiplexer_22 (
    .in0(memcell_41_parout), .in1(memcell_42_parout), .in2(memcell_43_parout), .in3(memcell_44_parout),
    .in4(fetcher_4_dout[3:0]), .in5(fourbit2_4_r0), .out(multiplexer_22_out),
    .sel({or_13_out[2], fetcher_4_dout[5], or_13_out[0]}));  // open: in6, in7
  Decoder #(.select(2)) decoder_20 (
    .out0(decoder_20_out0), .out1(decoder_20_out1), .out2(decoder_20_out2), .out3(decoder_20_out3),
    .sel(fetcher_6_dout[7:6]), .en(or_11_out));
  Multiplexer #(.select(3), .width(4)) multiplexer_23 (
    .in0(memcell_45_parout), .in1(memcell_46_parout), .in2(memcell_47_parout), .in3(memcell_48_parout),
    .in4(fetcher_3_dout[3:0]), .in5(fourbit2_3_r0), .out(multiplexer_23_out),
    .sel({or_12_out[2], fetcher_3_dout[5], or_12_out[0]}));  // open: in6, in7
  memcell memcell_41 (
    .Parlin(multiplexer_22_out), .Load(decoder_14_out0), .Serin(multiplexer_13_out), .Read(decoder_16_out0),
    .Write(decoder_18_out0), .ParOut(memcell_41_parout));  // open: SerOut
  memcell memcell_42 (
    .Parlin(multiplexer_22_out), .Load(decoder_14_out1), .Serin(multiplexer_13_out), .Read(decoder_16_out1),
    .Write(decoder_18_out1), .ParOut(memcell_42_parout));  // open: SerOut
  memcell memcell_43 (
    .Parlin(multiplexer_22_out), .Load(decoder_14_out2), .Serin(multiplexer_13_out), .Read(decoder_16_out2),
    .Write(decoder_18_out2), .ParOut(memcell_43_parout));  // open: SerOut
  memcell memcell_44 (
    .Parlin(multiplexer_22_out), .Load(decoder_14_out3), .Serin(multiplexer_13_out), .Read(decoder_16_out3),
    .Write(decoder_18_out3), .ParOut(memcell_44_parout));  // open: SerOut
  not not_14 (not_14_out, fetcher_5_dout[4]);
  and and_21 (and_21_out, not_14_out, fetcher_5_dout[10]);
  or or_14 (or_14_out, fetcher_5_dout[9], and_21_out);
  Decoder #(.select(2)) decoder_21 (
    .out0(decoder_21_out0), .out1(decoder_21_out1), .out2(decoder_21_out2), .out3(decoder_21_out3),
    .sel(fetcher_5_dout[7:6]), .en(or_14_out));
  not not_15 (not_15_out, fetcher_6_dout[10]);
  and and_22 (and_22_out, fetcher_6_dout[11], not_15_out);
  Decoder #(.select(2)) decoder_22 (
    .out0(decoder_22_out0), .out1(decoder_22_out1), .out2(decoder_22_out2), .out3(decoder_22_out3),
    .sel(fetcher_6_dout[5:4]), .en(and_22_out));
  memcell memcell_45 (
    .Parlin(multiplexer_23_out), .Load(decoder_15_out0), .Serin(multiplexer_12_out), .Read(decoder_17_out0),
    .Write(decoder_19_out0), .ParOut(memcell_45_parout));  // open: SerOut
  memcell memcell_46 (
    .Parlin(multiplexer_23_out), .Load(decoder_15_out1), .Serin(multiplexer_12_out), .Read(decoder_17_out1),
    .Write(decoder_19_out1), .ParOut(memcell_46_parout));  // open: SerOut
  memcell memcell_47 (
    .Parlin(multiplexer_23_out), .Load(decoder_15_out2), .Serin(multiplexer_12_out), .Read(decoder_17_out2),
    .Write(decoder_19_out2), .ParOut(memcell_47_parout));  // open: SerOut
  memcell memcell_48 (
    .Parlin(multiplexer_23_out), .Load(decoder_15_out3), .Serin(multiplexer_12_out), .Read(decoder_17_out3),
    .Write(decoder_19_out3), .ParOut(memcell_48_parout));  // open: SerOut
  not not_16 (not_16_out, fetcher_5_dout[10]);
  and and_23 (and_23_out, fetcher_5_dout[4], not_16_out);
  Decoder #(.select(2)) decoder_23 (
    .out0(decoder_23_out0), .out1(decoder_23_out1), .out2(decoder_23_out2), .out3(decoder_23_out3),
    .sel(fetcher_5_dout[5:4]), .en(and_23_out));
  LED led_21 (.in(fourbit2_5_r0[0]));
  Decoder #(.select(2)) decoder_24 (
    .out0(decoder_24_out0), .out1(decoder_24_out1), .out2(decoder_24_out2), .out3(decoder_24_out3),
    .sel(fetcher_6_dout[7:6]), .en(and_13_out));
  LED led_22 (.in(fourbit2_6_r0[0]));
  LED led_23 (.in(fourbit2_6_r0[1]));
  Decoder #(.select(2)) decoder_25 (
    .out0(decoder_25_out0), .out1(decoder_25_out1), .out2(decoder_25_out2), .out3(decoder_25_out3),
    .sel(fetcher_5_dout[7:6]), .en(and_12_out));
  fourbit2 fourbit2_5 (
    .Ain(multiplexer_26_out), .Bin(multiplexer_25_out), .Vo(fourbit2_5_vo), .R3(fourbit2_5_r0[3]),
    .R2(fourbit2_5_r0[2]), .R1(fourbit2_5_r0[1]), .R0(fourbit2_5_r0[0]));
  LED led_24 (.in(fourbit2_5_r0[1]));
  LED led_25 (.in(fourbit2_5_r0[2]));
  LED led_26 (.in(fourbit2_5_r0[3]));
  Multiplexer #(.select(3), .width(4)) multiplexer_24 (
    .in0(memcell_49_parout), .in1(memcell_50_parout), .in2(memcell_51_parout), .in3(memcell_52_parout),
    .in4(fetcher_6_dout[3:0]), .out(multiplexer_24_out), .sel({1'b0, fetcher_6_dout[5:4]}));  // open: in5, in6, in7
  LED led_27 (.in(fourbit2_6_vo));
  fourbit2 fourbit2_6 (
    .Ain(multiplexer_28_out), .Bin(multiplexer_24_out), .Vo(fourbit2_6_vo), .R3(fourbit2_6_r0[3]),
    .R2(fourbit2_6_r0[2]), .R1(fourbit2_6_r0[1]), .R0(fourbit2_6_r0[0]));
  LED led_28 (.in(fourbit2_6_r0[2]));
  LED led_29 (.in(fourbit2_6_r0[3]));
  and and_24 (and_24_out, fetcher_5_dout[10], not_17_out);
  not not_17 (not_17_out, fetcher_5_dout[11]);
  Multiplexer #(.select(3), .width(4)) multiplexer_25 (
    .in0(memcell_53_parout), .in1(memcell_54_parout), .in2(memcell_55_parout), .in3(memcell_56_parout),
    .in4(fetcher_5_dout[3:0]), .out(multiplexer_25_out), .sel({1'b0, fetcher_5_dout[5:4]}));  // open: in5, in6, in7
  Multiplexer #(.select(3), .width(4)) multiplexer_26 (
    .in0(memcell_53_parout), .in1(memcell_54_parout), .in2(memcell_55_parout), .in3(memcell_56_parout),
    .in4(fetcher_5_dout[3:0]), .out(multiplexer_26_out), .sel({1'b0, fetcher_5_dout[3:2]}));  // open: in5, in6, in7
  Multiplexer #(.select(3), .width(4)) multiplexer_27 (
    .in0(memcell_53_parout), .in1(memcell_54_parout), .in2(memcell_55_parout), .in3(memcell_56_parout),
    .in4(fourbit2_5_r0), .out(multiplexer_27_out));  // open: in5, in6, in7, sel
  LED led_30 (.in(fourbit2_5_vo));
  and and_25 (and_25_out, fetcher_6_dout[10], not_18_out);
  not not_18 (not_18_out, fetcher_6_dout[11]);
  or or_15 (or_18_out[2], and_25_out, fetcher_6_dout[8]);
  Multiplexer #(.select(3), .width(4)) multiplexer_28 (
    .in0(memcell_49_parout), .in1(memcell_50_parout), .in2(memcell_51_parout), .in3(memcell_52_parout),
    .in4(fetcher_6_dout[3:0]), .out(multiplexer_28_out), .sel({1'b0, fetcher_6_dout[3:2]}));  // open: in5, in6, in7
  Multiplexer #(.select(3), .width(4)) multiplexer_29 (
    .in0(memcell_49_parout), .in1(memcell_50_parout), .in2(memcell_51_parout), .in3(memcell_52_parout),
    .in4(fourbit2_6_r0), .out(multiplexer_29_out));  // open: in5, in6, in7, sel
  or or_16 (or_17_out[2], and_24_out, fetcher_5_dout[8]);
  Hex_Digit_Display hex_digit_display_52 (.value(memcell_49_parout));  // open: dp
  Hex_Digit_Display hex_digit_display_53 (.value(memcell_50_parout));  // open: dp
  Hex_Digit_Display hex_digit_display_54 (.value(memcell_51_parout));  // open: dp
  Hex_Digit_Display hex_digit_display_55 (.value(memcell_52_parout));  // open: dp
  or or_17 (or_17_out[0], and_24_out, fetcher_5_dout[4]);
  Hex_Digit_Display hex_digit_display_56 (.value(memcell_53_parout));  // open: dp
  Hex_Digit_Display hex_digit_display_57 (.value(memcell_54_parout));  // open: dp
  Hex_Digit_Display hex_digit_display_58 (.value(memcell_55_parout));  // open: dp
  Hex_Digit_Display hex_digit_display_59 (.value(memcell_56_parout));  // open: dp
  or or_18 (or_18_out[0], and_25_out, fetcher_6_dout[4]);
  Multiplexer #(.select(3), .width(4)) multiplexer_30 (
    .in0(memcell_49_parout), .in1(memcell_50_parout), .in2(memcell_51_parout), .in3(memcell_52_parout),
    .in4(fetcher_6_dout[3:0]), .in5(fourbit2_6_r0), .out(multiplexer_30_out),
    .sel({or_18_out[2], fetcher_6_dout[5], or_18_out[0]}));  // open: in6, in7
  Multiplexer #(.select(3), .width(4)) multiplexer_31 (
    .in0(memcell_53_parout), .in1(memcell_54_parout), .in2(memcell_55_parout), .in3(memcell_56_parout),
    .in4(fetcher_5_dout[3:0]), .in5(fourbit2_5_r0), .out(multiplexer_31_out),
    .sel({or_17_out[2], fetcher_5_dout[5], or_17_out[0]}));  // open: in6, in7
  memcell memcell_49 (
    .Parlin(multiplexer_30_out), .Load(decoder_20_out0), .Serin(multiplexer_15_out), .Read(decoder_22_out0),
    .Write(decoder_24_out0), .ParOut(memcell_49_parout));  // open: SerOut
  memcell memcell_50 (
    .Parlin(multiplexer_30_out), .Load(decoder_20_out1), .Serin(multiplexer_15_out), .Read(decoder_22_out1),
    .Write(decoder_24_out1), .ParOut(memcell_50_parout));  // open: SerOut
  memcell memcell_51 (
    .Parlin(multiplexer_30_out), .Load(decoder_20_out2), .Serin(multiplexer_15_out), .Read(decoder_22_out2),
    .Write(decoder_24_out2), .ParOut(memcell_51_parout));  // open: SerOut
  memcell memcell_52 (
    .Parlin(multiplexer_30_out), .Load(decoder_20_out3), .Serin(multiplexer_15_out), .Read(decoder_22_out3),
    .Write(decoder_24_out3), .ParOut(memcell_52_parout));  // open: SerOut
  memcell memcell_53 (
    .Parlin(multiplexer_31_out), .Load(decoder_21_out0), .Serin(multiplexer_14_out), .Read(decoder_23_out0),
    .Write(decoder_25_out0), .ParOut(memcell_53_parout));  // open: SerOut
  memcell memcell_54 (
    .Parlin(multiplexer_31_out), .Load(decoder_21_out1), .Serin(multiplexer_14_out), .Read(decoder_23_out1),
    .Write(decoder_25_out1), .ParOut(memcell_54_parout));  // open: SerOut
  memcell memcell_55 (
    .Parlin(multiplexer_31_out), .Load(decoder_21_out2), .Serin(multiplexer_14_out), .Read(decoder_23_out2),
    .Write(decoder_25_out2), .ParOut(memcell_55_parout));  // open: SerOut
  memcell memcell_56 (
    .Parlin(multiplexer_31_out), .Load(decoder_21_out3), .Serin(multiplexer_14_out), .Read(decoder_23_out3),
    .Write(decoder_25_out3), .ParOut(memcell_56_parout));  // open: SerOut
  Button button_14 (.out(button_14_out));
  mydemux mydemux_20 (
    .Enable(1'b1), .C0(in_14), .C1(in_13), .Din(button_14_out), .D0(mydemux_20_d0), .D1(mydemux_20_d1),
    .D2(mydemux_20_d2), .D3(mydemux_20_d3));
  Button button_15 (.out(button_15_out));
  Button button_16 (.out(button_16_out));
  mydemux mydemux_21 (
    .Enable(decoder_26_out0), .C0(fetcher_7_dout[4]), .C1(fetcher_7_dout[5]), .Din(1'b1), .D0(mydemux_21_d0),
    .D1(mydemux_21_d1), .D2(mydemux_21_d2), .D3(mydemux_21_d3));
  mydemux mydemux_22 (
    .Enable(decoder_26_out1), .C0(fetcher_7_dout[5]), .C1(fetcher_7_dout[4]), .Din(1'b1), .D0(mydemux_22_d0),
    .D1(mydemux_22_d1), .D2(mydemux_22_d2), .D3(mydemux_22_d3));
  Button button_17 (.out(button_17_out));
  mydemux mydemux_23 (
    .Enable(decoder_27_out1), .C0(fetcher_8_dout[4]), .C1(fetcher_8_dout[5]), .Din(1'b1), .D0(mydemux_23_d0),
    .D1(mydemux_23_d1), .D2(mydemux_23_d2), .D3(mydemux_23_d3));
  mydemux mydemux_24 (
    .Enable(decoder_27_out0), .C0(fetcher_8_dout[4]), .C1(fetcher_8_dout[5]), .Din(1'b1), .D0(mydemux_24_d0),
    .D1(mydemux_24_d1), .D2(mydemux_24_d2), .D3(mydemux_24_d3));
  Hex_Digit_Display hex_digit_display_60 (.value(fetcher_7_count));  // open: dp
  mydemux mydemux_25 (
    .Enable(1'b1), .C0(in_36), .C1(in_35), .Din(button_15_out), .D0(mydemux_25_d0), .D1(mydemux_25_d1),
    .D2(mydemux_25_d2), .D3(mydemux_25_d3));
  Hex_Digit_Display hex_digit_display_61 (.value(fetcher_8_count));  // open: dp
  Fetcher fetcher_7 (
    .RST(button_16_out), .num0(undriven_35), .num1(undriven_34), .num2(undriven_36), .num3(undriven_37),
    .num4(undriven_38), .num5(undriven_39), .num6(undriven_40), .num7(undriven_41), .count(fetcher_7_count),
    .Dout(fetcher_7_dout));  // open: N
  Decoder decoder_26 (
    .out0(decoder_26_out0), .out1(decoder_26_out1), .sel(fetcher_7_dout[10]), .en(fetcher_7_dout[11]));
  Fetcher fetcher_8 (
    .RST(button_17_out), .num0(12'hc10), .num1(12'h240), .num2(12'h34a), .num3(12'h4c4),
    .count(fetcher_8_count), .Dout(fetcher_8_dout));  // open: N, num4, num5, num6, num7
  Decoder decoder_27 (
    .out0(decoder_27_out0), .out1(decoder_27_out1), .sel(fetcher_8_dout[10]), .en(fetcher_8_dout[11]));
  Hex_Digit_Display hex_digit_display_62 (.value(memcell_61_parout));  // open: dp
  Hex_Digit_Display hex_digit_display_63 (.value(memcell_62_parout));  // open: dp
  Hex_Digit_Display hex_digit_display_64 (.value(memcell_63_parout));  // open: dp
  Hex_Digit_Display hex_digit_display_65 (.value(memcell_64_parout));  // open: dp
  and and_26 (and_26_out, fetcher_7_dout[4], fetcher_7_dout[5]);
  Hex_Digit_Display hex_digit_display_66 (.value(memcell_57_parout));  // open: dp
  Hex_Digit_Display hex_digit_display_67 (.value(memcell_58_parout));  // open: dp
  Hex_Digit_Display hex_digit_display_68 (.value(memcell_59_parout));  // open: dp
  Hex_Digit_Display hex_digit_display_69 (.value(memcell_60_parout));  // open: dp
  and and_27 (and_27_out, fetcher_8_dout[11], fetcher_8_dout[10]);
  memcell memcell_57 (
    .Parlin({in_15, in_16, in_17, in_18}), .Load(mydemux_20_d0), .Serin(parser_7_do), .Read(mydemux_21_d0),
    .Write(mydemux_22_d0), .SerOut(memcell_57_serout), .ParOut(memcell_57_parout));
  memcell memcell_58 (
    .Parlin({in_15, in_16, in_17, in_18}), .Load(mydemux_20_d1), .Serin(parser_7_do), .Read(mydemux_21_d1),
    .Write(mydemux_22_d1), .SerOut(memcell_58_serout), .ParOut(memcell_58_parout));
  memcell memcell_59 (
    .Parlin({in_15, in_16, in_17, in_18}), .Load(mydemux_20_d2), .Serin(parser_7_do), .Read(mydemux_21_d2),
    .Write(mydemux_22_d2), .SerOut(memcell_59_serout), .ParOut(memcell_59_parout));
  memcell memcell_60 (
    .Parlin({in_15, in_16, in_17, in_18}), .Load(mydemux_20_d3), .Serin(parser_7_do), .Read(mydemux_21_d3),
    .Write(mydemux_22_d3), .SerOut(memcell_60_serout), .ParOut(memcell_60_parout));
  memcell memcell_61 (
    .Parlin({in_29, in_30, in_31, in_32}), .Load(mydemux_25_d0), .Serin(parser_8_do), .Read(mydemux_23_d0),
    .Write(mydemux_24_d0), .SerOut(memcell_61_serout), .ParOut(memcell_61_parout));
  memcell memcell_62 (
    .Parlin({in_29, in_30, in_31, in_32}), .Load(mydemux_25_d1), .Serin(parser_8_do), .Read(mydemux_23_d1),
    .Write(mydemux_24_d1), .SerOut(memcell_62_serout), .ParOut(memcell_62_parout));
  memcell memcell_63 (
    .Parlin({in_29, in_30, in_31, in_32}), .Load(mydemux_25_d2), .Serin(parser_8_do), .Read(mydemux_23_d2),
    .Write(mydemux_24_d2), .SerOut(memcell_63_serout), .ParOut(memcell_63_parout));
  memcell memcell_64 (
    .Parlin({in_29, in_30, in_31, in_32}), .Load(mydemux_25_d3), .Serin(parser_8_do), .Read(mydemux_23_d3),
    .Write(mydemux_24_d3), .SerOut(memcell_64_serout), .ParOut(memcell_64_parout));
  Clock clock_4 ();  // open: out
  Multiplexer #(.select(2)) multiplexer_32 (
    .in0(memcell_61_serout), .in1(memcell_62_serout), .in2(memcell_63_serout), .in3(memcell_64_serout),
    .out(multiplexer_32_out), .sel(fetcher_8_dout[5:4]));
  Multiplexer #(.select(2)) multiplexer_33 (
    .in0(memcell_57_serout), .in1(memcell_58_serout), .in2(memcell_59_serout), .in3(memcell_60_serout),
    .out(multiplexer_33_out), .sel(fetcher_7_dout[5:4]));
  parser parser_7 (.Din(multiplexer_35_out), .Do(parser_7_do));
  parser parser_8 (.Din(multiplexer_37_out), .Do(parser_8_do));
  not not_19 (not_19_out, fetcher_8_dout[11]);
  and and_28 (and_28_out, not_19_out, fetcher_8_dout[10]);
  or or_19 (or_19_out, fetcher_8_dout[9], and_28_out);
  Decoder #(.select(2)) decoder_28 (
    .out0(decoder_28_out0), .out1(decoder_28_out1), .out2(decoder_28_out2), .out3(decoder_28_out3),
    .sel(fetcher_8_dout[7:6]), .en(or_19_out));
  not not_20 (not_20_out, fetcher_7_dout[4]);
  and and_29 (and_29_out, not_20_out, fetcher_7_dout[10]);
  or or_20 (or_20_out, fetcher_7_dout[9], and_29_out);
  Decoder #(.select(2)) decoder_29 (
    .out0(decoder_29_out0), .out1(decoder_29_out1), .out2(decoder_29_out2), .out3(decoder_29_out3),
    .sel(fetcher_7_dout[7:6]), .en(or_20_out));
  not not_21 (not_21_out, fetcher_8_dout[10]);
  and and_30 (and_30_out, fetcher_8_dout[11], not_21_out);
  Decoder #(.select(2)) decoder_30 (
    .out0(decoder_30_out0), .out1(decoder_30_out1), .out2(decoder_30_out2), .out3(decoder_30_out3),
    .sel(fetcher_8_dout[5:4]), .en(and_30_out));
  not not_22 (not_22_out, fetcher_7_dout[10]);
  and and_31 (and_31_out, fetcher_7_dout[4], not_22_out);
  Decoder #(.select(2)) decoder_31 (
    .out0(decoder_31_out0), .out1(decoder_31_out1), .out2(decoder_31_out2), .out3(decoder_31_out3),
    .sel(fetcher_7_dout[5:4]), .en(and_31_out));
  Decoder #(.select(2)) decoder_32 (
    .out0(decoder_32_out0), .out1(decoder_32_out1), .out2(decoder_32_out2), .out3(decoder_32_out3),
    .sel(fetcher_7_dout[7:6]), .en(and_26_out));
  LED led_31 (.in(fourbit2_7_r0[0]));
  LED led_32 (.in(fourbit2_7_r0[1]));
  LED led_33 (.in(fourbit2_7_r0[2]));
  LED led_34 (.in(fourbit2_7_r0[3]));
  Decoder #(.select(2)) decoder_33 (
    .out0(decoder_33_out0), .out1(decoder_33_out1), .out2(decoder_33_out2), .out3(decoder_33_out3),
    .sel(fetcher_8_dout[7:6]), .en(and_27_out));
  Multiplexer #(.select(3), .width(4)) multiplexer_34 (
    .in0(memcell_65_parout), .in1(memcell_66_parout), .in2(memcell_67_parout), .in3(memcell_68_parout),
    .in4(fetcher_8_dout[3:0]), .out(multiplexer_34_out), .sel({1'b0, fetcher_8_dout[5:4]}));  // open: in5, in6, in7
  LED led_35 (.in(fourbit2_8_r0[0]));
  LED led_36 (.in(fourbit2_8_r0[1]));
  LED led_37 (.in(fourbit2_8_r0[2]));
  LED led_38 (.in(fourbit2_8_r0[3]));
  and and_32 (and_32_out, fetcher_7_dout[10], not_23_out);
  not not_23 (not_23_out, fetcher_7_dout[11]);
  Multiplexer #(.select(3), .width(4)) multiplexer_35 (
    .in0(memcell_69_parout), .in1(memcell_70_parout), .in2(memcell_71_parout), .in3(memcell_72_parout),
    .in4(fourbit2_7_r0), .out(multiplexer_35_out));  // open: in5, in6, in7, sel
  LED led_39 (.in(fourbit2_7_vo));
  fourbit2 fourbit2_7 (
    .Ain(multiplexer_39_out), .Bin(multiplexer_38_out), .Vo(fourbit2_7_vo), .R3(fourbit2_7_r0[3]),
    .R2(fourbit2_7_r0[2]), .R1(fourbit2_7_r0[1]), .R0(fourbit2_7_r0[0]));
  and and_33 (and_33_out, fetcher_8_dout[10], not_24_out);
  not not_24 (not_24_out, fetcher_8_dout[11]);
  Multiplexer #(.select(3), .width(4)) multiplexer_36 (
    .in0(memcell_65_parout), .in1(memcell_66_parout), .in2(memcell_67_parout), .in3(memcell_68_parout),
    .in4(fetcher_8_dout[3:0]), .out(multiplexer_36_out), .sel({1'b0, fetcher_8_dout[3:2]}));  // open: in5, in6, in7
  Multiplexer #(.select(3), .width(4)) multiplexer_37 (
    .in0(memcell_65_parout), .in1(memcell_66_parout), .in2(memcell_67_parout), .in3(memcell_68_parout),
    .in4(fourbit2_8_r0), .out(multiplexer_37_out));  // open: in5, in6, in7, sel
  LED led_40 (.in(fourbit2_8_vo));
  fourbit2 fourbit2_8 (
    .Ain(multiplexer_36_out), .Bin(multiplexer_34_out), .Vo(fourbit2_8_vo), .R3(fourbit2_8_r0[3]),
    .R1(fourbit2_8_r0[1]), .R0(fourbit2_8_r0[0]));  // open: R2
  or or_21 (or_23_out[2], and_32_out, fetcher_7_dout[8]);
  Multiplexer #(.select(3), .width(4)) multiplexer_38 (
    .in0(memcell_69_parout), .in1(memcell_70_parout), .in2(memcell_71_parout), .in3(memcell_72_parout),
    .in4(fetcher_7_dout[3:0]), .out(multiplexer_38_out), .sel({1'b0, fetcher_7_dout[5:4]}));  // open: in5, in6, in7
  Multiplexer #(.select(3), .width(4)) multiplexer_39 (
    .in0(memcell_69_parout), .in1(memcell_70_parout), .in2(memcell_71_parout), .in3(memcell_72_parout),
    .in4(fetcher_7_dout[3:0]), .out(multiplexer_39_out), .sel({1'b0, fetcher_7_dout[3:2]}));  // open: in5, in6, in7
  or or_22 (or_24_out[2], and_33_out, fetcher_8_dout[8]);
  or or_23 (or_23_out[0], and_32_out, fetcher_7_dout[4]);
  or or_24 (or_24_out[0], and_33_out, fetcher_8_dout[4]);
  Hex_Digit_Display hex_digit_display_70 (.value(memcell_65_parout));  // open: dp
  Hex_Digit_Display hex_digit_display_71 (.value(memcell_66_parout));  // open: dp
  Hex_Digit_Display hex_digit_display_72 (.value(memcell_67_parout));  // open: dp
  Hex_Digit_Display hex_digit_display_73 (.value(memcell_68_parout));  // open: dp
  Multiplexer #(.select(3), .width(4)) multiplexer_40 (
    .in0(memcell_69_parout), .in1(memcell_70_parout), .in2(memcell_71_parout), .in3(memcell_72_parout),
    .in4(fetcher_7_dout[3:0]), .in5(fourbit2_7_r0), .out(multiplexer_40_out),
    .sel({or_23_out[2], fetcher_7_dout[5], or_23_out[0]}));  // open: in6, in7
  Hex_Digit_Display hex_digit_display_74 (.value(memcell_69_parout));  // open: dp
  Hex_Digit_Display hex_digit_display_75 (.value(memcell_70_parout));  // open: dp
  Hex_Digit_Display hex_digit_display_76 (.value(memcell_71_parout));  // open: dp
  Hex_Digit_Display hex_digit_display_77 (.value(memcell_72_parout));  // open: dp
  Multiplexer #(.select(3), .width(4)) multiplexer_41 (
    .in0(memcell_65_parout), .in1(memcell_66_parout), .in2(memcell_67_parout), .in3(memcell_68_parout),
    .in4(fetcher_8_dout[3:0]), .in5(fourbit2_8_r0), .out(multiplexer_41_out),
    .sel({or_24_out[2], fetcher_8_dout[5], or_24_out[0]}));  // open: in6, in7
  memcell memcell_65 (
    .Parlin(multiplexer_41_out), .Load(decoder_28_out0), .Serin(multiplexer_32_out), .Read(decoder_30_out0),
    .Write(decoder_33_out0), .ParOut(memcell_65_parout));  // open: SerOut
  memcell memcell_66 (
    .Parlin(multiplexer_41_out), .Load(decoder_28_out1), .Serin(multiplexer_32_out), .Read(decoder_30_out1),
    .Write(decoder_33_out1), .ParOut(memcell_66_parout));  // open: SerOut
  memcell memcell_67 (
    .Parlin(multiplexer_41_out), .Load(decoder_28_out2), .Serin(multiplexer_32_out), .Read(decoder_30_out2),
    .Write(decoder_33_out2), .ParOut(memcell_67_parout));  // open: SerOut
  memcell memcell_68 (
    .Parlin(multiplexer_41_out), .Load(decoder_28_out3), .Serin(multiplexer_32_out), .Read(decoder_30_out3),
    .Write(decoder_33_out3), .ParOut(memcell_68_parout));  // open: SerOut
  memcell memcell_69 (
    .Parlin(multiplexer_40_out), .Load(decoder_29_out0), .Serin(multiplexer_33_out), .Read(decoder_31_out0),
    .Write(decoder_32_out0), .ParOut(memcell_69_parout));  // open: SerOut
  memcell memcell_70 (
    .Parlin(multiplexer_40_out), .Load(decoder_29_out1), .Serin(multiplexer_33_out), .Read(decoder_31_out1),
    .Write(decoder_32_out1), .ParOut(memcell_70_parout));  // open: SerOut
  memcell memcell_71 (
    .Parlin(multiplexer_40_out), .Load(decoder_29_out2), .Serin(multiplexer_33_out), .Read(decoder_31_out2),
    .Write(decoder_32_out2), .ParOut(memcell_71_parout));  // open: SerOut
  memcell memcell_72 (
    .Parlin(multiplexer_40_out), .Load(decoder_29_out3), .Serin(multiplexer_33_out), .Read(decoder_31_out3),
    .Write(decoder_32_out3), .ParOut(memcell_72_parout));  // open: SerOut

  // Notes on the sheet:
  //   VALUE
  //   ADDRESS
  //   READ TO MEMORY
  //   WRITE TO MEMORY
  //   READ TO MEMORY
  //   WRITE TO MEMORY
  //   LDR RX,MY = 1100 XX YY 0000
  //   MOV RX,RY = 0010 XX YY 0000
  //   VALUE
  //   ADDRESS
  //   READ TO MEMORY
  //   WRITE TO MEMORY
  //   VALUE
  //   ADDRESS
  //   READ TO MEMORY
  //   WRITE TO MEMORY
  //   LDR RX,MY = 1100 XX YY 0000
  //   MOV RX,RY = 0010 XX YY 0000
  //   LDR RX,MY = 1100 XX YY 0000
  //   MOV RX,RY = 0010 XX YY 0000
  //   VALUE
  //   ADDRESS
  //   READ TO MEMORY
  //   WRITE TO MEMORY
  //   LDR RX,MY = 1100 XX YY 0000
  //   MOV RX,RY = 0010 XX YY 0000
endmodule
module MiniComputer (
  input  in_1,
  input  in_2,
  input  in_3,
  input  in_4,
  input  in_5,
  input  in_6,
  input  in_7,
  input  in_8,
  input  in_9,
  input  in_10,
  input  in_11,
  input  in_12,
  input  in_13,
  input  in_14,
  input  in_15,
  input  in_16,
  input  in_17,
  input  in_18,
  input  in_19,
  input  in_20,
  input  in_21,
  input  in_22,
  input  in_23,
  input  in_24,
  input  in_25,
  input  in_26,
  input  in_27,
  input  in_28,
  input  in_29,
  input  in_30,
  input  in_31,
  input  in_32,
  input  in_33,
  input  in_34,
  input  in_35,
  input  in_36,
  input  in_37,
  input  in_38,
  input  in_39,
  input  in_40,
  input  in_41,
  input  in_42,
  input  in_43,
  input  in_44,
  input  in_45,
  input  in_46,
  input  in_47,
  input  in_48,
  input  in_49,
  input  in_50,
  input  in_51
);

  wire and_1_out, and_2_out, and_3_out, and_4_out, button_1_out, button_2_out, button_3_out,
       memcell_1_serout, memcell_2_serout, memcell_3_serout, memcell_4_serout, memcell_5_serout,
       memcell_6_serout, minimux_1_dout, minimux_2_dout, mydemux_1_d0, mydemux_1_d1, mydemux_1_d2,
       mydemux_1_d3, mydemux_2_d0, mydemux_2_d1, mydemux_2_d2, mydemux_2_d3, mydemux_3_d0, mydemux_3_d1,
       mydemux_4_d0, mydemux_4_d1, mydemux_4_d2, mydemux_4_d3, mydemux_5_d0, mydemux_5_d1, mydemux_5_d2,
       mydemux_5_d3, mydemux_6_d0, mydemux_6_d1, mydemux_6_d2, mydemux_6_d3, or_1_out, parser_1_do,
       parser_2_do, parser_3_do, parser_4_do;
  wire [3:0] divider_1_out, fourbit_1_sum, fourbit_2_sum, memcell_1_parout, memcell_2_parout,
       memcell_3_parout, memcell_4_parout, memcell_5_parout, memcell_6_parout, memcell_7_parout,
       memcell_8_parout, memcell_9_parout, memcell_10_parout, multiplexer_1_out, multiplier_1_out,
       mux4_1_dout, mux4_2_dout, mux4_3_dout, mux4_4_dout, mux4_5_dout, mux4_6_dout, mux4_7_dout,
       mux4_8_dout, mux4_9_dout, mux4_10_dout, subtractor_1_out;

  Button button_1 (.out(button_1_out));
  mydemux mydemux_1 (
    .Enable(1'b1), .C0(in_8), .C1(in_7), .Din(button_1_out), .D0(mydemux_1_d0), .D1(mydemux_1_d1),
    .D2(mydemux_1_d2), .D3(mydemux_1_d3));
  Button button_2 (.out(button_2_out));
  mydemux mydemux_2 (
    .Enable(in_3), .C0(in_2), .C1(in_1), .Din(in_3), .D0(mydemux_2_d0), .D1(mydemux_2_d1), .D2(mydemux_2_d2),
    .D3(mydemux_2_d3));
  Hex_Digit_Display hex_digit_display_1 (.value(memcell_1_parout));  // open: dp
  Hex_Digit_Display hex_digit_display_2 (.value(memcell_2_parout));  // open: dp
  Hex_Digit_Display hex_digit_display_3 (.value(memcell_3_parout));  // open: dp
  Hex_Digit_Display hex_digit_display_4 (.value(memcell_4_parout));  // open: dp
  Multiplexer #(.select(3), .width(4)) multiplexer_1 (
    .in0(memcell_1_parout), .in1(memcell_2_parout), .in2(memcell_3_parout), .in3(memcell_4_parout),
    .in4(memcell_5_parout), .in5(memcell_6_parout), .in6(multiplier_1_out), .in7(divider_1_out),
    .out(multiplexer_1_out), .sel({in_43, in_44, in_45}));
  Hex_Digit_Display hex_digit_display_5 (.value(multiplexer_1_out));  // open: dp
  mydemux mydemux_3 (
    .Enable(1'b1), .C0(in_36), .C1(in_35), .Din(button_2_out), .D0(mydemux_3_d0), .D1(mydemux_3_d1));  // open: D2, D3
  memcell memcell_1 (
    .Parlin({in_9, in_10, in_11, in_12}), .Load(mydemux_1_d0), .Read(mydemux_2_d0),
    .SerOut(memcell_1_serout), .ParOut(memcell_1_parout));  // open: Serin, Write
  memcell memcell_2 (
    .Parlin({in_9, in_10, in_11, in_12}), .Load(mydemux_1_d1), .Read(mydemux_2_d1),
    .SerOut(memcell_2_serout), .ParOut(memcell_2_parout));  // open: Serin, Write
  memcell memcell_3 (
    .Parlin({in_9, in_10, in_11, in_12}), .Load(mydemux_1_d2), .Read(mydemux_2_d2),
    .SerOut(memcell_3_serout), .ParOut(memcell_3_parout));  // open: Serin, Write
  memcell memcell_4 (
    .Parlin({in_9, in_10, in_11, in_12}), .Load(mydemux_1_d3), .Read(mydemux_2_d3),
    .SerOut(memcell_4_serout), .ParOut(memcell_4_parout));  // open: Serin, Write
  Hex_Digit_Display hex_digit_display_6 (.value(memcell_5_parout));  // open: dp
  Hex_Digit_Display hex_digit_display_7 (.value(memcell_6_parout));  // open: dp
  memcell memcell_5 (
    .Parlin({in_25, in_26, in_27, in_28}), .Load(mydemux_3_d0), .SerOut(memcell_5_serout),
    .ParOut(memcell_5_parout));  // open: Serin, Read, Write
  memcell memcell_6 (
    .Parlin({in_29, in_30, in_31, in_32}), .Load(mydemux_3_d1), .SerOut(memcell_6_serout),
    .ParOut(memcell_6_parout));  // open: Serin, Read, Write
  minimux minimux_1 (
    .C0(in_2), .C1(in_1), .D0(memcell_1_serout), .D1(memcell_2_serout), .D2(memcell_3_serout),
    .D3(memcell_4_serout), .Dout(minimux_1_dout));
  or or_1 (or_1_out, and_4_out, and_3_out, and_2_out, and_1_out);
  mydemux mydemux_4 (
    .Enable(in_4), .C0(in_6), .C1(in_5), .Din(in_4), .D0(mydemux_4_d0), .D1(mydemux_4_d1), .D2(mydemux_4_d2),
    .D3(mydemux_4_d3));
  minimux minimux_2 (
    .C0(in_3), .C1(in_16), .D0(or_1_out), .D1(minimux_1_dout), .D2(memcell_5_serout), .D3(memcell_6_serout),
    .Dout(minimux_2_dout));
  Button button_3 (.out(button_3_out));
  mydemux mydemux_5 (
    .Enable(1'b1), .C0(in_40), .C1(in_39), .Din(button_3_out), .D0(mydemux_5_d0), .D1(mydemux_5_d1),
    .D2(mydemux_5_d2), .D3(mydemux_5_d3));
  Hex_Digit_Display hex_digit_display_8 (.value(memcell_7_parout));  // open: dp
  Hex_Digit_Display hex_digit_display_9 (.value(memcell_8_parout));  // open: dp
  Hex_Digit_Display hex_digit_display_10 (.value(memcell_9_parout));  // open: dp
  Hex_Digit_Display hex_digit_display_11 (.value(memcell_10_parout));  // open: dp
  memcell memcell_7 (
    .Parlin(fourbit_1_sum), .Load(mydemux_5_d0), .Serin(minimux_2_dout), .Write(mydemux_4_d0),
    .ParOut(memcell_7_parout));  // open: Read, SerOut
  memcell memcell_8 (
    .Parlin(fourbit_1_sum), .Load(mydemux_5_d1), .Serin(minimux_2_dout), .Write(mydemux_4_d1),
    .ParOut(memcell_8_parout));  // open: Read, SerOut
  memcell memcell_9 (
    .Parlin(fourbit_1_sum), .Load(mydemux_5_d2), .Serin(minimux_2_dout), .Write(mydemux_4_d2),
    .ParOut(memcell_9_parout));  // open: Read, SerOut
  memcell memcell_10 (
    .Parlin(fourbit_1_sum), .Load(mydemux_5_d3), .Serin(minimux_2_dout), .Write(mydemux_4_d3),
    .ParOut(memcell_10_parout));  // open: Read, SerOut
  Hex_Digit_Display hex_digit_display_12 (.value(fourbit_1_sum));  // open: dp
  Hex_Digit_Display hex_digit_display_13 (.value(mux4_1_dout));  // open: dp
  Hex_Digit_Display hex_digit_display_14 (.value(mux4_2_dout));  // open: dp
  Hex_Digit_Display hex_digit_display_15 (.value(mux4_3_dout));  // open: dp
  mux4 mux4_1 (
    .C0(in_14), .C1(in_13), .D0(memcell_7_parout), .D1(memcell_8_parout), .D2(memcell_9_parout),
    .D3(memcell_10_parout), .Dout(mux4_1_dout));
  mux4 mux4_2 (
    .C0(in_20), .C1(in_19), .D0(memcell_7_parout), .D1(memcell_8_parout), .D2(memcell_9_parout),
    .D3(memcell_10_parout), .Dout(mux4_2_dout));
  Hex_Digit_Display hex_digit_display_16 (.value(mux4_4_dout));  // open: dp
  Hex_Digit_Display hex_digit_display_17 (.value(mux4_5_dout));  // open: dp
  Hex_Digit_Display hex_digit_display_18 (.value(mux4_6_dout));  // open: dp
  Hex_Digit_Display hex_digit_display_19 (.value(mux4_7_dout));  // open: dp
  Hex_Digit_Display hex_digit_display_20 (.value(mux4_8_dout));  // open: dp
  fourbit fourbit_1 (.Ain(mux4_1_dout), .Bin(mux4_2_dout), .Sum(fourbit_1_sum));  // open: Co
  mux4 mux4_3 (
    .C0(in_22), .C1(in_21), .D0(memcell_7_parout), .D1(memcell_8_parout), .D2(memcell_9_parout),
    .D3(memcell_10_parout), .Dout(mux4_3_dout));
  mux4 mux4_4 (
    .C0(in_34), .C1(in_33), .D0(memcell_7_parout), .D1(memcell_8_parout), .D2(memcell_9_parout),
    .D3(memcell_10_parout), .Dout(mux4_4_dout));
  mux4 mux4_5 (
    .C0(in_42), .C1(in_41), .D0(memcell_7_parout), .D1(memcell_8_parout), .D2(memcell_9_parout),
    .D3(memcell_10_parout), .Dout(mux4_5_dout));
  mux4 mux4_6 (
    .C0(in_47), .C1(in_46), .D0(memcell_7_parout), .D1(memcell_8_parout), .D2(memcell_9_parout),
    .D3(memcell_10_parout), .Dout(mux4_6_dout));
  mux4 mux4_7 (
    .C0(in_49), .C1(in_48), .D0(memcell_7_parout), .D1(memcell_8_parout), .D2(memcell_9_parout),
    .D3(memcell_10_parout), .Dout(mux4_7_dout));
  mux4 mux4_8 (
    .C0(in_51), .C1(in_50), .D0(memcell_7_parout), .D1(memcell_8_parout), .D2(memcell_9_parout),
    .D3(memcell_10_parout), .Dout(mux4_8_dout));
  Hex_Digit_Display hex_digit_display_21 (.value(subtractor_1_out));  // open: dp
  Subtractor #(.width(4)) subtractor_1 (.a(mux4_3_dout), .b(mux4_4_dout), .out(subtractor_1_out));  // open: bin, bout
  Hex_Digit_Display hex_digit_display_22 (.value(multiplier_1_out));  // open: dp
  Multiplier #(.width(4)) multiplier_1 (.a(mux4_5_dout), .b(mux4_6_dout), .out(multiplier_1_out));  // open: cin, cout
  Hex_Digit_Display hex_digit_display_23 (.value(divider_1_out));  // open: dp
  Divider #(.width(4)) divider_1 (.a(mux4_7_dout), .b(mux4_8_dout), .out(divider_1_out));  // open: upper, rem
  parser parser_1 (.Din(fourbit_1_sum), .Do(parser_1_do));
  and and_1 (and_1_out, parser_1_do, mydemux_6_d0);
  parser parser_2 (.Din(subtractor_1_out), .Do(parser_2_do));
  and and_2 (and_2_out, parser_2_do, mydemux_6_d1);
  parser parser_3 (.Din(multiplier_1_out), .Do(parser_3_do));
  parser parser_4 (.Din(divider_1_out), .Do(parser_4_do));
  and and_3 (and_3_out, parser_3_do, mydemux_6_d2);
  and and_4 (and_4_out, parser_4_do, mydemux_6_d3);
  mydemux mydemux_6 (
    .Enable(in_15), .C0(in_18), .C1(in_17), .Din(in_15), .D0(mydemux_6_d0), .D1(mydemux_6_d1),
    .D2(mydemux_6_d2), .D3(mydemux_6_d3));
  Hex_Digit_Display hex_digit_display_24 (.value(mux4_9_dout));  // open: dp
  Hex_Digit_Display hex_digit_display_25 (.value(mux4_10_dout));  // open: dp
  mux4 mux4_9 (
    .C0(in_24), .C1(in_23), .D0(fourbit_1_sum), .D1(subtractor_1_out), .D2(multiplier_1_out),
    .D3(divider_1_out), .Dout(mux4_9_dout));
  mux4 mux4_10 (
    .C0(in_38), .C1(in_37), .D0(fourbit_1_sum), .D1(subtractor_1_out), .D2(multiplier_1_out),
    .D3(divider_1_out), .Dout(mux4_10_dout));
  Hex_Digit_Display hex_digit_display_26 (.value(fourbit_2_sum));  // open: dp
  fourbit fourbit_2 (.Ain(mux4_9_dout), .Bin(mux4_10_dout), .Sum(fourbit_2_sum));  // open: Co

  // Notes on the sheet:
  //   ADDRESS
  //   READ
  //   VALUE
  //   MEM0
  //   MEM1
  //   MEM2
  //   MEM3
  //   READ
  //   SOURCE
  //   SOURCE
  //   WRITE
  //   DESTINSTION
  //   CPU
  //   REG0
  //   REG1
  //   REG2
  //   REG3
  //   ADD
  //   SUB
  //   ALU
  //   PRO
  //   DIV
endmodule
