// Logisim project computersystemassignment.circ as structural Verilog: 7 circuits, main circuit main
module main (
  input  bit4
);

  wire button_1_out, button_2_out, button_3_out, clock_1_out, t_ff_1_q;
  wire [3:0] counters_1_outm1, counters_1_outm2, counters_1_outs1, counters_1_outs2,
       shift_registers_1_st1outputm1, shift_registers_1_st1outputm2, shift_registers_1_st1outputs1,
       shift_registers_1_st1outputs2, shift_registers_1_st2outputm1, shift_registers_1_st2outputm2,
       shift_registers_1_st2outputs1, shift_registers_1_st2outputs2, shift_registers_1_st3outputm1,
       shift_registers_1_st3outputm2, shift_registers_1_st3outputs1, shift_registers_1_st3outputs2,
       shift_registers_1_st4outputm1, shift_registers_1_st4outputm2, shift_registers_1_st4outputs1,
       shift_registers_1_st4outputs2, shift_registers_1_st5outputm1, shift_registers_1_st5outputm2,
       shift_registers_1_st5outputs1, shift_registers_1_st5outputs2;

  Hex_Digit_Display hex_digit_display_1 (.value(counters_1_outm2));  // open: dp
  Hex_Digit_Display hex_digit_display_2 (.value(counters_1_outm1));  // open: dp
  Button button_1 (.out(button_1_out));
  Hex_Digit_Display hex_digit_display_3 (.value(counters_1_outs2));  // open: dp
  Hex_Digit_Display hex_digit_display_4 (.value(counters_1_outs1));  // open: dp
  Button button_2 (.out(button_2_out));
  Button button_3 (.out(button_3_out));
  Hex_Digit_Display hex_digit_display_5 (.value(shift_registers_1_st1outputm2));  // open: dp
  Hex_Digit_Display hex_digit_display_6 (.value(shift_registers_1_st1outputm1));  // open: dp
  Shift_Registers shift_registers_1 (
    .InputM2(counters_1_outm2), .inputM1(counters_1_outm1), .InputS2(counters_1_outs2),
    .InputS1(counters_1_outs1), .InputT(t_ff_1_q), .Split(button_2_out), .Reset(button_3_out),
    .ST1OutputM2(shift_registers_1_st1outputm2), .ST1OutputM1(shift_registers_1_st1outputm1),
    .ST1OutputS2(shift_registers_1_st1outputs2), .ST1OutputS1(shift_registers_1_st1outputs1),
    .ST2OutputM2(shift_registers_1_st2outputm2), .ST2OutputM1(shift_registers_1_st2outputm1),
    .ST2OutputS2(shift_registers_1_st2outputs2), .ST2OutputS1(shift_registers_1_st2outputs1),
    .ST3OutputM2(shift_registers_1_st3outputm2), .ST3OutputM1(shift_registers_1_st3outputm1),
    .ST3OutputS2(shift_registers_1_st3outputs2), .ST3OutputS1(shift_registers_1_st3outputs1),
    .ST4OutputM2(shift_registers_1_st4outputm2), .ST4OutputM1(shift_registers_1_st4outputm1),
    .ST4OutputS2(shift_registers_1_st4outputs2), .ST4OutputS1(shift_registers_1_st4outputs1),
    .ST5OutputM2(shift_registers_1_st5outputm2), .ST5OutputM1(shift_registers_1_st5outputm1),
    .ST5OutputS2(shift_registers_1_st5outputs2), .ST5OutputS1(shift_registers_1_st5outputs1));
  LED led_1 (.in(t_ff_1_q));
  Hex_Digit_Display hex_digit_display_7 (.value(shift_registers_1_st1outputs2));  // open: dp
  Hex_Digit_Display hex_digit_display_8 (.value(shift_registers_1_st1outputs1));  // open: dp
  T_Flip_Flop t_ff_1 (.clk(button_1_out), .T(1'b1), .Q(t_ff_1_q), .reset(button_3_out));  // open: Qn, preset
  Clock clock_1 (.out(clock_1_out));
  Counters counters_1 (
    .InputS(t_ff_1_q), .Clock(clock_1_out), .bit4(bit4), .Reset(button_3_out), .OutS1(counters_1_outs1),
    .OutS2(counters_1_outs2), .OutM1(counters_1_outm1), .OutM2(counters_1_outm2));
  Hex_Digit_Display hex_digit_display_9 (.value(shift_registers_1_st2outputm2));  // open: dp
  Hex_Digit_Display hex_digit_display_10 (.value(shift_registers_1_st2outputm1));  // open: dp
  Hex_Digit_Display hex_digit_display_11 (.value(shift_registers_1_st2outputs2));  // open: dp
  Hex_Digit_Display hex_digit_display_12 (.value(shift_registers_1_st2outputs1));  // open: dp
  Hex_Digit_Display hex_digit_display_13 (.value(shift_registers_1_st3outputm2));  // open: dp
  Hex_Digit_Display hex_digit_display_14 (.value(shift_registers_1_st3outputm1));  // open: dp
  Hex_Digit_Display hex_digit_display_15 (.value(shift_registers_1_st3outputs2));  // open: dp
  Hex_Digit_Display hex_digit_display_16 (.value(shift_registers_1_st3outputs1));  // open: dp
  Hex_Digit_Display hex_digit_display_17 (.value(shift_registers_1_st4outputm2));  // open: dp
  Hex_Digit_Display hex_digit_display_18 (.value(shift_registers_1_st4outputm1));  // open: dp
  Hex_Digit_Display hex_digit_display_19 (.value(shift_registers_1_st4outputs2));  // open: dp
  Hex_Digit_Display hex_digit_display_20 (.value(shift_registers_1_st4outputs1));  // open: dp
  Hex_Digit_Display hex_digit_display_21 (.value(shift_registers_1_st5outputm2));  // open: dp
  Hex_Digit_Display hex_digit_display_22 (.value(shift_registers_1_st5outputm1));  // open: dp
  Hex_Digit_Display hex_digit_display_23 (.value(shift_registers_1_st5outputs2));  // open: dp
  Hex_Digit_Display hex_digit_display_24 (.value(shift_registers_1_st5outputs1));  // open: dp

  // Notes on the sheet:
  //   Elapsed Time
  //   Minutes
  //   :
  //   Start / Stop
  //   Seconds
  //   Stopwatch Interface
  //   Split
  //   Reset
  //   Minutes
  //   Clock Started
  //   Split Time
  //   :
  //   Seconds
  //   Split Time 2
  //   Minutes
  //   :
  //   Seconds
  //   Split Time 3
  //   Minutes
  //   :
  //   Seconds
  //   Split Time 4
  //   Minutes
  //   :
  //   Seconds
  //   Minutes
  //   Split Time 5
  //   :
  //   Seconds
endmodule

module counter0_to_5 (
  input  InputCount,
  input  Reset,
  input  Clock,
  input  bit4,
  output [3:0] Outputcount,
  output clocktrigger
);

  wire and_1_out, and_2_out, and_3_out, j_k_ff_1_q, j_k_ff_2_q, j_k_ff_3_q, or_1_out;

  and and_1 (and_1_out, InputCount, Clock);
  J_K_Flip_Flop j_k_ff_1 (
    .J(InputCount), .K(InputCount), .clk(and_1_out), .Q(j_k_ff_1_q), .reset(or_1_out));  // open: Qn, preset
  J_K_Flip_Flop j_k_ff_2 (
    .J(j_k_ff_1_q), .K(j_k_ff_1_q), .clk(and_1_out), .Q(j_k_ff_2_q), .reset(or_1_out));  // open: Qn, preset
  D_Flip_Flop #(.trigger("falling")) d_ff_1 (
    .D(j_k_ff_1_q), .clk(and_1_out), .Q(Outputcount[0]), .reset(Reset));  // open: Qn, preset
  and and_2 (and_2_out, j_k_ff_1_q, j_k_ff_2_q);
  J_K_Flip_Flop j_k_ff_3 (
    .J(and_2_out), .K(and_2_out), .clk(and_1_out), .Q(j_k_ff_3_q), .reset(or_1_out));  // open: Qn, preset
  D_Flip_Flop #(.trigger("falling")) d_ff_2 (
    .D(j_k_ff_2_q), .clk(and_1_out), .Q(Outputcount[1]), .reset(Reset));  // open: Qn, preset
  D_Flip_Flop #(.trigger("falling")) d_ff_3 (
    .D(j_k_ff_3_q), .clk(and_1_out), .Q(Outputcount[2]), .reset(Reset));  // open: Qn, preset
  and and_3 (and_3_out, j_k_ff_2_q, j_k_ff_3_q);
  or or_1 (or_1_out, and_3_out, Reset);
  and and_4 (clocktrigger, Outputcount[2], Outputcount[0]);

  assign Outputcount[3] = bit4;
endmodule

module counter0_to_9 (
  input  InputCount,
  input  Reset,
  input  Clock,
  output [3:0] Outputcount,
  output clocktrigger
);

  wire and_1_out, and_2_out, and_3_out, and_4_out, j_k_ff_1_q, j_k_ff_2_q, j_k_ff_3_q, j_k_ff_4_q, or_1_out;

  and and_1 (and_1_out, InputCount, Clock);
  J_K_Flip_Flop j_k_ff_1 (
    .J(InputCount), .K(InputCount), .clk(and_1_out), .Q(j_k_ff_1_q), .reset(or_1_out));  // open: Qn, preset
  J_K_Flip_Flop j_k_ff_2 (
    .J(j_k_ff_1_q), .K(j_k_ff_1_q), .clk(and_1_out), .Q(j_k_ff_2_q), .reset(or_1_out));  // open: Qn, preset
  D_Flip_Flop #(.trigger("falling")) d_ff_1 (
    .D(j_k_ff_1_q), .clk(and_1_out), .Q(Outputcount[0]), .reset(Reset));  // open: Qn, preset
  and and_2 (and_2_out, j_k_ff_1_q, j_k_ff_2_q);
  J_K_Flip_Flop j_k_ff_3 (
    .J(and_2_out), .K(and_2_out), .clk(and_1_out), .Q(j_k_ff_3_q), .reset(or_1_out));  // open: Qn, preset
  D_Flip_Flop #(.trigger("falling")) d_ff_2 (
    .D(j_k_ff_2_q), .clk(and_1_out), .Q(Outputcount[1]), .reset(Reset));  // open: Qn, preset
  and and_3 (and_3_out, and_2_out, j_k_ff_3_q);
  J_K_Flip_Flop j_k_ff_4 (
    .J(and_3_out), .K(and_3_out), .clk(and_1_out), .Q(j_k_ff_4_q), .reset(or_1_out));  // open: Qn, preset
  D_Flip_Flop #(.trigger("falling")) d_ff_3 (
    .D(j_k_ff_3_q), .clk(and_1_out), .Q(Outputcount[2]), .reset(Reset));  // open: Qn, preset
  D_Flip_Flop #(.trigger("falling")) d_ff_4 (
    .D(j_k_ff_4_q), .clk(and_1_out), .Q(Outputcount[3]), .reset(Reset));  // open: Qn, preset
  and and_4 (and_4_out, j_k_ff_2_q, j_k_ff_4_q);
  or or_1 (or_1_out, and_4_out, Reset);
  and and_5 (clocktrigger, Outputcount[3], Outputcount[0]);
endmodule

module Counters (
  input  InputS,
  input  Clock,
  input  bit4,
  input  Reset,
  output [3:0] OutS1,
  output [3:0] OutS2,
  output [3:0] OutM1,
  output [3:0] OutM2
);

  wire counter0_to_5_1_clocktrigger, counter0_to_9_1_clocktrigger, counter0_to_9_2_clocktrigger;

  counter0_to_9 counter0_to_9_1 (
    .InputCount(InputS), .Reset(Reset), .Clock(Clock), .Outputcount(OutS1),
    .clocktrigger(counter0_to_9_1_clocktrigger));
  counter0_to_5 counter0_to_5_1 (
    .InputCount(1'b1), .Reset(Reset), .Clock(counter0_to_9_1_clocktrigger), .bit4(bit4), .Outputcount(OutS2),
    .clocktrigger(counter0_to_5_1_clocktrigger));
  counter0_to_9 counter0_to_9_2 (
    .InputCount(1'b1), .Reset(Reset), .Clock(counter0_to_5_1_clocktrigger), .Outputcount(OutM1),
    .clocktrigger(counter0_to_9_2_clocktrigger));
  counter0_to_9 counter0_to_9_3 (
    .InputCount(1'b1), .Reset(Reset), .Clock(counter0_to_9_2_clocktrigger), .Outputcount(OutM2));  // open: clocktrigger
endmodule

module Registers (
  input  [3:0] InputT,
  input  Clock,
  input  Reset,
  output [3:0] OutputT
);

  D_Flip_Flop d_ff_1 (.D(InputT[0]), .clk(Clock), .Q(OutputT[0]), .reset(Reset));  // open: Qn, preset
  D_Flip_Flop d_ff_2 (.D(InputT[1]), .clk(Clock), .Q(OutputT[1]), .reset(Reset));  // open: Qn, preset
  D_Flip_Flop d_ff_3 (.D(InputT[2]), .clk(Clock), .Q(OutputT[2]), .reset(Reset));  // open: Qn, preset
  D_Flip_Flop d_ff_4 (.D(InputT[3]), .clk(Clock), .Q(OutputT[3]), .reset(Reset));  // open: Qn, preset
endmodule

module Registers_as_a_whole (
  input  [3:0] InputM2,
  input  [3:0] InputM1,
  input  [3:0] InputS2,
  input  [3:0] InputS1,
  input  Clock,
  input  Reset,
  output [3:0] OutM2,
  output [3:0] OutM1,
  output [3:0] OutS2,
  output [3:0] OutS1
);

  Registers registers_1 (.InputT(InputM2), .Clock(Clock), .Reset(Reset), .OutputT(OutM2));
  Registers registers_2 (.InputT(InputM1), .Clock(Clock), .Reset(Reset), .OutputT(OutM1));
  Registers registers_3 (.InputT(InputS2), .Clock(Clock), .Reset(Reset), .OutputT(OutS2));
  Registers registers_4 (.InputT(InputS1), .Clock(Clock), .Reset(Reset), .OutputT(OutS1));
endmodule

module Shift_Registers (
  input  [3:0] InputM2,
  input  [3:0] inputM1,
  input  [3:0] InputS2,
  input  [3:0] InputS1,
  input  InputT,
  input  Split,
  input  Reset,
  output [3:0] ST1OutputM2,
  output [3:0] ST1OutputM1,
  output [3:0] ST1OutputS2,
  output [3:0] ST1OutputS1,
  output [3:0] ST2OutputM2,
  output [3:0] ST2OutputM1,
  output [3:0] ST2OutputS2,
  output [3:0] ST2OutputS1,
  output [3:0] ST3OutputM2,
  output [3:0] ST3OutputM1,
  output [3:0] ST3OutputS2,
  output [3:0] ST3OutputS1,
  output [3:0] ST4OutputM2,
  output [3:0] ST4OutputM1,
  output [3:0] ST4OutputS2,
  output [3:0] ST4OutputS1,
  output [3:0] ST5OutputM2,
  output [3:0] ST5OutputM1,
  output [3:0] ST5OutputS2,
  output [3:0] ST5OutputS1
);

  wire and_1_out;

  and and_1 (and_1_out, InputT, 1'b1, Split);
  Registers_as_a_whole registers_as_a_whole_1 (
    .InputM2(InputM2), .InputM1(inputM1), .InputS2(InputS2), .InputS1(InputS1), .Clock(and_1_out),
    .Reset(Reset), .OutM2(ST1OutputM2), .OutM1(ST1OutputM1), .OutS2(ST1OutputS2), .OutS1(ST1OutputS1));
  Registers_as_a_whole registers_as_a_whole_2 (
    .InputM2(ST1OutputM2), .InputM1(ST1OutputM1), .InputS2(ST1OutputS2), .InputS1(ST1OutputS1),
    .Clock(and_1_out), .Reset(Reset), .OutM2(ST2OutputM2), .OutM1(ST2OutputM1), .OutS2(ST2OutputS2),
    .OutS1(ST2OutputS1));
  Registers_as_a_whole registers_as_a_whole_3 (
    .InputM2(ST2OutputM2), .InputM1(ST2OutputM1), .InputS2(ST2OutputS2), .InputS1(ST2OutputS1),
    .Clock(and_1_out), .Reset(Reset), .OutM2(ST3OutputM2), .OutM1(ST3OutputM1), .OutS2(ST3OutputS2),
    .OutS1(ST3OutputS1));
  Registers_as_a_whole registers_as_a_whole_4 (
    .InputM2(ST3OutputM2), .InputM1(ST3OutputM1), .InputS2(ST3OutputS2), .InputS1(ST3OutputS1),
    .Clock(and_1_out), .Reset(Reset), .OutM2(ST4OutputM2), .OutM1(ST4OutputM1), .OutS2(ST4OutputS2),
    .OutS1(ST4OutputS1));
  Registers_as_a_whole registers_as_a_whole_5 (
    .InputM2(ST4OutputM2), .InputM1(ST4OutputM1), .InputS2(ST4OutputS2), .InputS1(ST4OutputS1),
    .Clock(and_1_out), .Reset(Reset), .OutM2(ST5OutputM2), .OutM1(ST5OutputM1), .OutS2(ST5OutputS2),
    .OutS1(ST5OutputS1));
endmodule
