// Logisim project lab06.circ as structural Verilog: 18 circuits, main circuit fourbit
module fourbit (
  input  [3:0] Ain,
  input  [3:0] Bin,
  output [3:0] Sum,
  output Co
);

  wire fulladder_1_cout, fulladder_2_cout, halfadder_1_cout;

  halfadder halfadder_1 (.InputA(Ain[0]), .InputB(Bin[0]), .numout(Sum[0]), .Cout(halfadder_1_cout));
  fulladder fulladder_1 (.Cin(halfadder_1_cout), .A(Ain[1]), .B(Bin[1]), .numout(Sum[1]), .Cout(fulladder_1_cout));
  fulladder fulladder_2 (.Cin(fulladder_1_cout), .A(Ain[2]), .B(Bin[2]), .numout(Sum[2]), .Cout(fulladder_2_cout));
  fulladder fulladder_3 (.Cin(fulladder_2_cout), .A(Ain[3]), .B(Bin[3]), .numout(Sum[3]), .Cout(Co));
endmodule

module fulladder (
  input  Cin,
  input  A,
  input  B,
  output numout,
  output Cout
);

  wire and_1_out, and_2_out, xor_1_out;

  xor xor_1 (xor_1_out, A, B);
  and and_1 (and_1_out, A, B);
  xor xor_2 (numout, Cin, xor_1_out);
  and and_2 (and_2_out, Cin, xor_1_out);
  or or_1 (Cout, and_2_out, and_1_out);
endmodule

module halfadder (
  input  InputA,
  input  InputB,
  output numout,
  output Cout
);

  xor xor_1 (numout, InputA, InputB);
  and and_1 (Cout, InputA, InputB);
endmodule

module main (
  input  Reset,
  input  Clk,
  input  writeEnable,
  input  in_4,
  input  in_5,
  input  ReadEnable,
  input  in_7,
  input  in_8,
  input  in_9,
  input  in_10,
  input  in_11,
  input  in_12,
  input  in_13,
  input  in_14,
  input  in_15,
  input  in_16,
  input  in_17,
  input  in_18,
  input  in_19,
  input  in_20,
  input  in_21,
  input  in_22,
  input  in_23
);

  wire button_1_out, LOAD_out, MEM0_serout, MEM1_serout, MEM2_serout, MEM3_serout, minimux_1_dout,
       mydemux_1_d0, mydemux_1_d1, mydemux_1_d2, mydemux_1_d3, mydemux_2_d0, mydemux_2_d1, mydemux_2_d2,
       mydemux_2_d3, mydemux_3_d0, mydemux_3_d1, mydemux_3_d2, mydemux_3_d3, mydemux_4_d0, mydemux_4_d1,
       mydemux_4_d2, mydemux_4_d3, mydemux_5_d0, mydemux_5_d1, mydemux_5_d2, mydemux_5_d3, parser_1_do,
       SOURCE_dout;
  wire [1:0] count_1_cout;
  wire [3:0] demux4_1_d0, demux4_1_d1, demux4_1_d2, demux4_1_d3, fourbit_1_sum, MEM0_parout, MEM1_parout,
       MEM2_parout, MEM3_parout, memcell_1_parout, memcell_2_parout, memcell_3_parout, memcell_4_parout,
       mux4_1_dout, mux4_2_dout, REG0_parout, REG1_parout, REG2_parout, REG3_parout;

  Button LOAD (.out(LOAD_out));
  mydemux mydemux_1 (
    .Enable(1'b1), .C0(in_18), .C1(in_17), .Din(LOAD_out), .D0(mydemux_1_d0), .D1(mydemux_1_d1),
    .D2(mydemux_1_d2), .D3(mydemux_1_d3));
  mydemux mydemux_2 (
    .Enable(ReadEnable), .C0(in_8), .C1(in_7), .Din(ReadEnable), .D0(mydemux_2_d0), .D1(mydemux_2_d1),
    .D2(mydemux_2_d2), .D3(mydemux_2_d3));
  Hex_Digit_Display hex_digit_display_1 (.value(MEM0_parout));  // open: dp
  Hex_Digit_Display hex_digit_display_2 (.value(MEM1_parout));  // open: dp
  Hex_Digit_Display hex_digit_display_3 (.value(MEM2_parout));  // open: dp
  Hex_Digit_Display hex_digit_display_4 (.value(MEM3_parout));  // open: dp
  memcell MEM0 (
    .Parlin({in_13, in_14, in_15, in_16}), .Load(mydemux_1_d0), .Read(mydemux_2_d0), .SerOut(MEM0_serout),
    .ParOut(MEM0_parout));  // open: Serin, Write
  memcell MEM1 (
    .Parlin({in_13, in_14, in_15, in_16}), .Load(mydemux_1_d1), .Read(mydemux_2_d1), .SerOut(MEM1_serout),
    .ParOut(MEM1_parout));  // open: Serin, Write
  memcell MEM2 (
    .Parlin({in_13, in_14, in_15, in_16}), .Load(mydemux_1_d2), .Read(mydemux_2_d2), .SerOut(MEM2_serout),
    .ParOut(MEM2_parout));  // open: Serin, Write
  memcell MEM3 (
    .Parlin({in_13, in_14, in_15, in_16}), .Load(mydemux_1_d3), .Read(mydemux_2_d3), .SerOut(MEM3_serout),
    .ParOut(MEM3_parout));  // open: Serin, Write
  minimux SOURCE (
    .C0(in_8), .C1(in_7), .D0(MEM0_serout), .D1(MEM1_serout), .D2(MEM2_serout), .D3(MEM3_serout),
    .Dout(SOURCE_dout));
  minimux minimux_1 (
    .C0(ReadEnable), .C1(in_21), .D0(parser_1_do), .D1(SOURCE_dout), .Dout(minimux_1_dout));  // open: D2, D3
  mydemux mydemux_3 (
    .Enable(writeEnable), .C0(in_5), .C1(in_4), .Din(minimux_1_dout), .D0(mydemux_3_d0), .D1(mydemux_3_d1),
    .D2(mydemux_3_d2), .D3(mydemux_3_d3));
  mydemux mydemux_4 (
    .Enable(writeEnable), .C0(in_5), .C1(in_4), .Din(writeEnable), .D0(mydemux_4_d0), .D1(mydemux_4_d1),
    .D2(mydemux_4_d2), .D3(mydemux_4_d3));
  Clock clock_1 ();  // open: out
  Hex_Digit_Display hex_digit_display_5 (.value(REG0_parout));  // open: dp
  Hex_Digit_Display hex_digit_display_6 (.value(REG1_parout));  // open: dp
  Hex_Digit_Display hex_digit_display_7 (.value(REG2_parout));  // open: dp
  Hex_Digit_Display hex_digit_display_8 (.value(REG3_parout));  // open: dp
  memcell REG0 (.Serin(mydemux_3_d0), .Write(mydemux_4_d0), .ParOut(REG0_parout));  // open: Parlin, Load, Read, SerOut
  memcell REG1 (.Serin(mydemux_3_d1), .Write(mydemux_4_d1), .ParOut(REG1_parout));  // open: Parlin, Load, Read, SerOut
  memcell REG2 (.Serin(mydemux_3_d2), .Write(mydemux_4_d2), .ParOut(REG2_parout));  // open: Parlin, Load, Read, SerOut
  memcell REG3 (.Serin(mydemux_3_d3), .Write(mydemux_4_d3), .ParOut(REG3_parout));  // open: Parlin, Load, Read, SerOut
  Hex_Digit_Display hex_digit_display_9 (.value(fourbit_1_sum));  // open: dp
  mux4 mux4_1 (
    .C0(in_10), .C1(in_9), .D0(REG0_parout), .D1(REG1_parout), .D2(REG2_parout), .D3(REG3_parout),
    .Dout(mux4_1_dout));
  mux4 mux4_2 (
    .C0(in_23), .C1(in_22), .D0(REG0_parout), .D1(REG1_parout), .D2(REG2_parout), .D3(REG3_parout),
    .Dout(mux4_2_dout));
  Button button_1 (.out(button_1_out));
  fourbit fourbit_1 (.Ain(mux4_1_dout), .Bin(mux4_2_dout), .Sum(fourbit_1_sum));  // open: Co
  mydemux mydemux_5 (
    .Enable(1'b1), .C0(in_20), .C1(in_19), .Din(button_1_out), .D0(mydemux_5_d0), .D1(mydemux_5_d1),
    .D2(mydemux_5_d2), .D3(mydemux_5_d3));
  demux4 demux4_1 (
    .CP0(in_20), .CP1(in_19), .Din(fourbit_1_sum), .D0(demux4_1_d0), .D1(demux4_1_d1), .D2(demux4_1_d2),
    .D3(demux4_1_d3));
  Hex_Digit_Display hex_digit_display_10 (.value(memcell_1_parout));  // open: dp
  Hex_Digit_Display hex_digit_display_11 (.value(memcell_2_parout));  // open: dp
  Hex_Digit_Display hex_digit_display_12 (.value(memcell_3_parout));  // open: dp
  Hex_Digit_Display hex_digit_display_13 (.value(memcell_4_parout));  // open: dp
  count count_1 (.Clk(Clk), .Reset(Reset), .Cout(count_1_cout));
  memcell memcell_1 (
    .Parlin(demux4_1_d0), .Load(mydemux_5_d0), .ParOut(memcell_1_parout));  // open: Serin, Read, Write, SerOut
  memcell memcell_2 (
    .Parlin(demux4_1_d1), .Load(mydemux_5_d1), .ParOut(memcell_2_parout));  // open: Serin, Read, Write, SerOut
  memcell memcell_3 (
    .Parlin(demux4_1_d2), .Load(mydemux_5_d2), .ParOut(memcell_3_parout));  // open: Serin, Read, Write, SerOut
  memcell memcell_4 (
    .Parlin(demux4_1_d3), .Load(mydemux_5_d3), .ParOut(memcell_4_parout));  // open: Serin, Read, Write, SerOut
  Hex_Digit_Display hex_digit_display_14 (.value({in_11, in_12, count_1_cout}));  // open: dp
  parser parser_1 (.Din(fourbit_1_sum), .Do(parser_1_do));

  // Notes on the sheet:
  //   ADDRESS
  //   VALUE
  //   SOURCE
  //   Destination
  //   ALU vs MEM
  //   redundant
  //   It needs 8 bits to register from the sum as first four bits clear the previous value and then the next four bits inserts the sum value or output. But if you want the change in just 4 bits then remove the redundant mydemux circuit and then connect the Dout the minimux to all the serial inputs of the memory cells
  //   CPU
  //   ADD
endmodule

module mymux (
  input  A1,
  input  A0,
  input  [3:0] Din,
  output Dout
);

  wire and_1_out, and_2_out, and_3_out, and_4_out, and_5_out, and_6_out, and_7_out, nor_1_out, not_1_out,
       not_2_out;

  nor nor_1 (nor_1_out, A0, A1);
  and and_1 (and_1_out, A0, not_1_out);
  not not_1 (not_1_out, A1);
  not not_2 (not_2_out, A0);
  and and_2 (and_2_out, not_2_out, A1);
  and and_3 (and_3_out, A0, A1);
  and and_4 (and_4_out, nor_1_out, Din[0]);
  and and_5 (and_5_out, Din[1], and_1_out);
  and and_6 (and_6_out, and_2_out, Din[2]);
  and and_7 (and_7_out, Din[3], and_3_out);
  or or_1 (Dout, and_4_out, and_5_out, and_6_out, and_7_out);
endmodule

module minimux (
  input  C0,
  input  C1,
  input  D0,
  input  D1,
  input  D2,
  input  D3,
  output Dout
);

  wire and_1_out, and_2_out, and_3_out, and_4_out, not_1_out, not_2_out, not_3_out, not_4_out;

  not not_1 (not_1_out, C0);
  not not_2 (not_2_out, C1);
  not not_3 (not_3_out, C1);
  not not_4 (not_4_out, C0);
  and and_1 (and_1_out, not_1_out, not_2_out, D0);
  and and_2 (and_2_out, not_3_out, C0, D1);
  and and_3 (and_3_out, C1, not_4_out, D2);
  and and_4 (and_4_out, C1, C0, D3);
  or or_1 (Dout, and_1_out, and_2_out, and_3_out, and_4_out);
endmodule

module mux4 (
  input  C0,
  input  C1,
  input  [3:0] D0,
  input  [3:0] D1,
  input  [3:0] D2,
  input  [3:0] D3,
  output [3:0] Dout
);

  minimux minimux_1 (.C0(C0), .C1(C1), .D0(D0[0]), .D1(D1[0]), .D2(D2[0]), .D3(D3[0]), .Dout(Dout[0]));
  minimux minimux_2 (.C0(C0), .C1(C1), .D0(D0[1]), .D1(D1[1]), .D2(D2[1]), .D3(D3[1]), .Dout(Dout[1]));
  minimux minimux_3 (.C0(C0), .C1(C1), .D0(D0[2]), .D1(D1[2]), .D2(D2[2]), .D3(D3[2]), .Dout(Dout[2]));
  minimux minimux_4 (.C0(C0), .C1(C1), .D0(D0[3]), .D1(D1[3]), .D2(D2[3]), .D3(D3[3]), .Dout(Dout[3]));
endmodule

module mydemux (
  input  Enable,
  input  C0,
  input  C1,
  input  Din,
  output D0,
  output D1,
  output D2,
  output D3
);

  wire and_1_out, not_1_out, not_2_out, not_3_out, not_4_out;

  and and_1 (and_1_out, Enable, Din);
  not not_1 (not_1_out, C0);
  not not_2 (not_2_out, C1);
  not not_3 (not_3_out, C1);
  not not_4 (not_4_out, C0);
  and and_2 (D0, not_1_out, not_2_out, and_1_out);
  and and_3 (D1, not_3_out, C0, and_1_out);
  and and_4 (D2, C1, not_4_out, and_1_out);
  and and_5 (D3, C1, C0, and_1_out);
endmodule

module memcell (
  input  [3:0] Parlin,
  input  Load,
  input  Serin,
  input  Read,
  input  Write,
  output SerOut,
  output [3:0] ParOut
);

  wire and_1_out, and_2_out, and_3_out, and_4_out, and_5_out, and_6_out, and_7_out, and_8_out, and_9_out,
       and_10_out, and_11_out, and_12_out, and_13_out, and_14_out, and_15_out, and_16_out, and_17_out,
       and_18_out, clock_1_out, clock_2_out, clock_3_out, clock_4_out, not_1_out, not_2_out, not_3_out,
       not_4_out, not_5_out, not_6_out, not_7_out, not_8_out, or_1_out, or_2_out;

  and and_1 (and_1_out, Write, Serin);
  and and_2 (and_2_out, ParOut[3], Read);
  or or_1 (or_1_out, Write, Read);
  or or_2 (or_2_out, and_1_out, and_2_out);
  not not_1 (not_1_out, or_2_out);
  and and_3 (and_3_out, or_1_out, or_2_out);
  and and_4 (and_4_out, or_1_out, not_1_out);
  J_K_Flip_Flop j_k_ff_1 (
    .J(and_3_out), .K(and_4_out), .clk(clock_1_out), .Q(ParOut[0]), .preset(and_5_out), .reset(and_6_out));  // open: Qn
  Clock clock_1 (.out(clock_1_out));
  and and_5 (and_5_out, Load, Parlin[0]);
  and and_6 (and_6_out, Load, not_2_out);
  not not_2 (not_2_out, Parlin[0]);
  and and_7 (and_7_out, or_1_out, ParOut[0]);
  and and_8 (and_8_out, or_1_out, not_3_out);
  not not_3 (not_3_out, ParOut[0]);
  Clock clock_2 (.out(clock_2_out));
  and and_9 (and_9_out, Load, Parlin[1]);
  J_K_Flip_Flop j_k_ff_2 (
    .J(and_7_out), .K(and_8_out), .clk(clock_2_out), .Q(ParOut[1]), .preset(and_9_out), .reset(and_10_out));  // open: Qn
  and and_10 (and_10_out, Load, not_4_out);
  not not_4 (not_4_out, Parlin[1]);
  and and_11 (and_11_out, or_1_out, ParOut[1]);
  and and_12 (and_12_out, or_1_out, not_5_out);
  not not_5 (not_5_out, ParOut[1]);
  Clock clock_3 (.out(clock_3_out));
  J_K_Flip_Flop j_k_ff_3 (
    .J(and_11_out), .K(and_12_out), .clk(clock_3_out), .Q(ParOut[2]), .preset(and_13_out), .reset(and_14_out));  // open: Qn
  and and_13 (and_13_out, Load, Parlin[2]);
  and and_14 (and_14_out, Load, not_6_out);
  not not_6 (not_6_out, Parlin[2]);
  and and_15 (and_15_out, or_1_out, ParOut[2]);
  and and_16 (and_16_out, or_1_out, not_7_out);
  not not_7 (not_7_out, ParOut[2]);
  Clock clock_4 (.out(clock_4_out));
  and and_17 (and_17_out, Load, Parlin[3]);
  J_K_Flip_Flop j_k_ff_4 (
    .J(and_15_out), .K(and_16_out), .clk(clock_4_out), .Q(ParOut[3]), .preset(and_17_out), .reset(and_18_out));  // open: Qn
  and and_18 (and_18_out, Load, not_8_out);
  not not_8 (not_8_out, Parlin[3]);

  assign SerOut = ParOut[3];
endmodule

module demux4 (
  input  CP0,
  input  CP1,
  input  [3:0] Din,
  output [3:0] D0,
  output [3:0] D1,
  output [3:0] D2,
  output [3:0] D3
);

  mydemux mydemux_1 (.Enable(1'b1), .C0(CP0), .C1(CP1), .Din(Din[0]), .D0(D0[0]), .D1(D1[0]), .D2(D2[0]), .D3(D3[0]));
  mydemux mydemux_2 (.Enable(1'b1), .C0(CP0), .C1(CP1), .Din(Din[1]), .D0(D0[1]), .D1(D1[1]), .D2(D2[1]), .D3(D3[1]));
  mydemux mydemux_3 (.Enable(1'b1), .C0(CP0), .C1(CP1), .Din(Din[2]), .D0(D0[2]), .D1(D1[2]), .D2(D2[2]), .D3(D3[2]));
  mydemux mydemux_4 (.Enable(1'b1), .C0(CP0), .C1(CP1), .Din(Din[3]), .D0(D0[3]), .D1(D1[3]), .D2(D2[3]), .D3(D3[3]));
endmodule

module count (
  input  Clk,
  input  Reset,
  output [1:0] Cout
);

  wire and_1_out, or_1_out, t_ff_1_q, t_ff_2_q, t_ff_3_q;

  T_Flip_Flop t_ff_1 (.T(1'b1), .clk(Clk), .Q(t_ff_1_q), .reset(or_1_out));  // open: Qn, preset
  D_Flip_Flop d_ff_1 (.D(t_ff_1_q), .clk(Clk), .Q(Cout[0]), .reset(Reset));  // open: Qn, preset
  T_Flip_Flop t_ff_2 (.T(t_ff_1_q), .clk(Clk), .Q(t_ff_2_q), .reset(or_1_out));  // open: Qn, preset
  D_Flip_Flop d_ff_2 (.D(t_ff_2_q), .clk(Clk), .Q(Cout[1]), .reset(Reset));  // open: Qn, preset
  and and_1 (and_1_out, t_ff_1_q, t_ff_2_q);
  T_Flip_Flop t_ff_3 (.T(and_1_out), .clk(Clk), .Q(t_ff_3_q), .reset(or_1_out));  // open: Qn, preset
  or or_1 (or_1_out, t_ff_3_q, Reset);
endmodule

module parser (
  input  [3:0] Din,
  output Do
);

  wire clock_1_out;
  wire [1:0] count_1_cout;

  Clock clock_1 (.out(clock_1_out));
  count count_1 (.Clk(clock_1_out), .Cout(count_1_cout));  // open: Reset
  minimux minimux_1 (
    .C0(count_1_cout[0]), .C1(count_1_cout[1]), .D0(Din[0]), .D1(Din[1]), .D2(Din[2]), .D3(Din[3]), .Dout(Do));
endmodule

module CPU (
  input  in_1,
  input  in_2,
  input  in_3,
  input  in_4,
  input  in_5,
  input  in_6
);

  wire and_1_out, and_2_out, and_3_out, and_4_out, button_1_out, decoder_1_out0, decoder_1_out1,
       decoder_2_out0, decoder_2_out1, decoder_2_out2, decoder_2_out3, decoder_3_out0, decoder_3_out1,
       decoder_3_out2, decoder_3_out3, decoder_4_out0, decoder_4_out1, decoder_4_out2, decoder_4_out3,
       fourbit2_1_vo, LOAD_out, memcell_1_serout, memcell_2_serout, memcell_3_serout, memcell_4_serout,
       multiplexer_1_out, mydemux_1_d0, mydemux_1_d1, mydemux_1_d2, mydemux_1_d3, not_1_out, not_2_out,
       not_3_out, or_1_out, parser_1_do, ReadingtoMem_d0, ReadingtoMem_d1, ReadingtoMem_d2, ReadingtoMem_d3,
       WritingToMem_d0, WritingToMem_d1, WritingToMem_d2, WritingToMem_d3;
  wire [1:0] PC_dout_2, PC_dout_3, PC_dout_4, PC_dout_5;
  wire [2:0] or_3_out;
  wire [3:0] fourbit2_1_r0, memcell_1_parout, memcell_2_parout, memcell_3_parout, memcell_4_parout,
       memcell_5_parout, memcell_6_parout, memcell_7_parout, memcell_8_parout, multiplexer_2_out,
       multiplexer_3_out, multiplexer_4_out, multiplexer_5_out, PC_out_11;
  wire [11:8] PC_dout;

  Button LOAD (.out(LOAD_out));
  mydemux ReadingtoMem (
    .Enable(decoder_1_out1), .C0(PC_dout_2[0]), .C1(PC_dout_2[1]), .Din(1'b1), .D0(ReadingtoMem_d0),
    .D1(ReadingtoMem_d1), .D2(ReadingtoMem_d2), .D3(ReadingtoMem_d3));
  mydemux WritingToMem (
    .Enable(decoder_1_out0), .C0(PC_dout_2[0]), .C1(PC_dout_2[1]), .Din(1'b1), .D0(WritingToMem_d0),
    .D1(WritingToMem_d1), .D2(WritingToMem_d2), .D3(WritingToMem_d3));
  Button button_1 (.out(button_1_out));
  mydemux mydemux_1 (
    .Enable(1'b1), .C0(in_6), .C1(in_5), .Din(LOAD_out), .D0(mydemux_1_d0), .D1(mydemux_1_d1),
    .D2(mydemux_1_d2), .D3(mydemux_1_d3));
  Hex_Digit_Display hex_digit_display_1 (.value(PC_out_11));  // open: dp
  Fetcher PC (
    .RST(button_1_out), .num0(12'hc10), .num1(12'h240), .num2(12'h34a), .num3(12'h4c4), .out_11(PC_out_11),
    .Dout({PC_dout, PC_dout_3, PC_dout_2, PC_dout_5, PC_dout_4}));  // open: N, num4, num5, num6, num7
  Decoder decoder_1 (.out0(decoder_1_out0), .out1(decoder_1_out1), .sel(PC_dout[10]), .en(PC_dout[11]));
  and and_1 (and_1_out, PC_dout[11], PC_dout[10]);
  Hex_Digit_Display hex_digit_display_2 (.value(memcell_1_parout));  // open: dp
  Hex_Digit_Display hex_digit_display_3 (.value(memcell_2_parout));  // open: dp
  Hex_Digit_Display hex_digit_display_4 (.value(memcell_3_parout));  // open: dp
  Hex_Digit_Display hex_digit_display_5 (.value(memcell_4_parout));  // open: dp
  memcell memcell_1 (
    .Parlin({in_1, in_2, in_3, in_4}), .Load(mydemux_1_d0), .Serin(parser_1_do), .Read(ReadingtoMem_d0),
    .Write(WritingToMem_d0), .SerOut(memcell_1_serout), .ParOut(memcell_1_parout));
  memcell memcell_2 (
    .Parlin({in_1, in_2, in_3, in_4}), .Load(mydemux_1_d1), .Serin(parser_1_do), .Read(ReadingtoMem_d1),
    .Write(WritingToMem_d1), .SerOut(memcell_2_serout), .ParOut(memcell_2_parout));
  memcell memcell_3 (
    .Parlin({in_1, in_2, in_3, in_4}), .Load(mydemux_1_d2), .Serin(parser_1_do), .Read(ReadingtoMem_d2),
    .Write(WritingToMem_d2), .SerOut(memcell_3_serout), .ParOut(memcell_3_parout));
  memcell memcell_4 (
    .Parlin({in_1, in_2, in_3, in_4}), .Load(mydemux_1_d3), .Serin(parser_1_do), .Read(ReadingtoMem_d3),
    .Write(WritingToMem_d3), .SerOut(memcell_4_serout), .ParOut(memcell_4_parout));
  Clock clock_1 ();  // open: out
  Multiplexer #(.select(2)) multiplexer_1 (
    .in0(memcell_1_serout), .in1(memcell_2_serout), .in2(memcell_3_serout), .in3(memcell_4_serout),
    .out(multiplexer_1_out), .sel(PC_dout_2));
  parser parser_1 (.Din(multiplexer_4_out), .Do(parser_1_do));
  not not_1 (not_1_out, PC_dout[11]);
  and and_2 (and_2_out, not_1_out, PC_dout[10]);
  or or_1 (or_1_out, PC_dout[9], and_2_out);
  Decoder #(.select(2)) decoder_2 (
    .out0(decoder_2_out0), .out1(decoder_2_out1), .out2(decoder_2_out2), .out3(decoder_2_out3),
    .sel(PC_dout_3), .en(or_1_out));
  not not_2 (not_2_out, PC_dout[10]);
  and and_3 (and_3_out, PC_dout[11], not_2_out);
  Decoder #(.select(2)) decoder_3 (
    .out0(decoder_3_out0), .out1(decoder_3_out1), .out2(decoder_3_out2), .out3(decoder_3_out3),
    .sel(PC_dout_2), .en(and_3_out));
  Decoder #(.select(2)) decoder_4 (
    .out0(decoder_4_out0), .out1(decoder_4_out1), .out2(decoder_4_out2), .out3(decoder_4_out3),
    .sel(PC_dout_3), .en(and_1_out));
  Multiplexer #(.select(3), .width(4)) multiplexer_2 (
    .in0(memcell_5_parout), .in1(memcell_6_parout), .in2(memcell_7_parout), .in3(memcell_8_parout),
    .in4({PC_dout_5, PC_dout_4}), .out(multiplexer_2_out), .sel({1'b0, PC_dout_2}));  // open: in5, in6, in7
  LED led_1 (.in(fourbit2_1_r0[0]));
  LED led_2 (.in(fourbit2_1_r0[1]));
  LED led_3 (.in(fourbit2_1_r0[2]));
  not not_3 (not_3_out, PC_dout[11]);
  LED led_4 (.in(fourbit2_1_vo));
  fourbit2 fourbit2_1 (
    .Ain(multiplexer_3_out), .Bin(multiplexer_2_out), .Vo(fourbit2_1_vo), .R3(fourbit2_1_r0[3]),
    .R2(fourbit2_1_r0[2]), .R1(fourbit2_1_r0[1]), .R0(fourbit2_1_r0[0]));
  LED led_5 (.in(fourbit2_1_r0[3]));
  and and_4 (and_4_out, PC_dout[10], not_3_out);
  or or_2 (or_3_out[2], and_4_out, PC_dout[8]);
  Multiplexer #(.select(3), .width(4)) multiplexer_3 (
    .in0(memcell_5_parout), .in1(memcell_6_parout), .in2(memcell_7_parout), .in3(memcell_8_parout),
    .in4({PC_dout_5, PC_dout_4}), .out(multiplexer_3_out), .sel({1'b0, PC_dout_5}));  // open: in5, in6, in7
  Multiplexer #(.select(3), .width(4)) multiplexer_4 (
    .in0(memcell_5_parout), .in1(memcell_6_parout), .in2(memcell_7_parout), .in3(memcell_8_parout),
    .in4(fourbit2_1_r0), .out(multiplexer_4_out));  // open: in5, in6, in7, sel
  or or_3 (or_3_out[0], and_4_out, PC_dout_2[0]);
  Hex_Digit_Display hex_digit_display_6 (.value(memcell_5_parout));  // open: dp
  Hex_Digit_Display hex_digit_display_7 (.value(memcell_6_parout));  // open: dp
  Hex_Digit_Display hex_digit_display_8 (.value(memcell_7_parout));  // open: dp
  Hex_Digit_Display hex_digit_display_9 (.value(memcell_8_parout));  // open: dp
  Multiplexer #(.select(3), .width(4)) multiplexer_5 (
    .in0(memcell_5_parout), .in1(memcell_6_parout), .in2(memcell_7_parout), .in3(memcell_8_parout),
    .in4({PC_dout_5, PC_dout_4}), .in5(fourbit2_1_r0), .out(multiplexer_5_out),
    .sel({or_3_out[2], PC_dout_2[1], or_3_out[0]}));  // open: in6, in7
  memcell memcell_5 (
    .Parlin(multiplexer_5_out), .Load(decoder_2_out0), .Serin(multiplexer_1_out), .Read(decoder_3_out0),
    .Write(decoder_4_out0), .ParOut(memcell_5_parout));  // open: SerOut
  memcell memcell_6 (
    .Parlin(multiplexer_5_out), .Load(decoder_2_out1), .Serin(multiplexer_1_out), .Read(decoder_3_out1),
    .Write(decoder_4_out1), .ParOut(memcell_6_parout));  // open: SerOut
  memcell memcell_7 (
    .Parlin(multiplexer_5_out), .Load(decoder_2_out2), .Serin(multiplexer_1_out), .Read(decoder_3_out2),
    .Write(decoder_4_out2), .ParOut(memcell_7_parout));  // open: SerOut
  memcell memcell_8 (
    .Parlin(multiplexer_5_out), .Load(decoder_2_out3), .Serin(multiplexer_1_out), .Read(decoder_3_out3),
    .Write(decoder_4_out3), .ParOut(memcell_8_parout));  // open: SerOut

  // Notes on the sheet:
  //   VALUE
  //   ADDRESS
  //   LDR RX,MY = 1100 XX YY 0000
  //   MOV RX,RY = 0010 XX YY 0000
endmodule

module Fetcher (
  input  N,
  input  RST,
  input  [11:0] num0,
  input  [11:0] num1,
  input  [11:0] num2,
  input  [11:0] num3,
  input  [11:0] num4,
  input  [11:0] num5,
  input  [11:0] num6,
  input  [11:0] num7,
  output [3:0] out_11,
  output [11:0] Dout
);

  wire clock_1_out;
  wire [1:0] count2_1_cout;

  Clock clock_1 (.out(clock_1_out));
  count2 count2_1 (.Clk(clock_1_out), .Reset(RST), .Cout(count2_1_cout));
  counter0_to_7 counter0_to_7_1 (.Clock(count2_1_cout[1]), .Reset(RST), .out_3(out_11[2:0]));
  Hex_Digit_Display hex_digit_display_1 (.value({2'b00, count2_1_cout}));  // open: dp
  Hex_Digit_Display hex_digit_display_2 (.value({N, out_11[2:0]}));  // open: dp
  mux12 mux12_1 (
    .num0(num0), .num1(num1), .num2(num2), .num3(num3), .num4(num4), .num5(num5), .num6(num6), .num7(num7),
    .Controlpins(out_11[2:0]), .Dout(Dout));

  assign out_11[3] = N;
endmodule

module mux12 (
  input  [11:0] num0,
  input  [11:0] num1,
  input  [11:0] num2,
  input  [11:0] num3,
  input  [11:0] num4,
  input  [11:0] num5,
  input  [11:0] num6,
  input  [11:0] num7,
  input  [2:0] Controlpins,
  output [11:0] Dout
);

  Multiplexer #(.select(3), .width(12)) multiplexer_1 (
    .in0(num0), .in1(num1), .in2(num2), .in3(num3), .in4(num4), .in5(num5), .in6(num6), .in7(num7),
    .out(Dout), .sel(Controlpins));
endmodule

module counter0_to_7 (
  input  Clock,
  input  Reset,
  output [2:0] out_3
);

  wire and_1_out, and_2_out, or_1_out, t_ff_1_q, t_ff_2_q, t_ff_3_q, t_ff_4_q;

  T_Flip_Flop t_ff_1 (.T(1'b1), .clk(Clock), .Q(t_ff_1_q), .reset(or_1_out));  // open: Qn, preset
  D_Flip_Flop #(.trigger("falling")) d_ff_1 (
    .D(t_ff_1_q), .clk(Clock), .Q(out_3[0]), .reset(Reset));  // open: Qn, preset
  T_Flip_Flop t_ff_2 (.T(t_ff_1_q), .clk(Clock), .Q(t_ff_2_q), .reset(or_1_out));  // open: Qn, preset
  and and_1 (and_1_out, t_ff_1_q, t_ff_2_q);
  T_Flip_Flop t_ff_3 (.T(and_1_out), .clk(Clock), .Q(t_ff_3_q), .reset(or_1_out));  // open: Qn, preset
  D_Flip_Flop #(.trigger("falling")) d_ff_2 (
    .D(t_ff_2_q), .clk(Clock), .Q(out_3[1]), .reset(Reset));  // open: Qn, preset
  and and_2 (and_2_out, and_1_out, t_ff_3_q);
  T_Flip_Flop t_ff_4 (.T(and_2_out), .clk(Clock), .Q(t_ff_4_q), .reset(or_1_out));  // open: Qn, preset
  D_Flip_Flop #(.trigger("falling")) d_ff_3 (
    .D(t_ff_3_q), .clk(Clock), .Q(out_3[2]), .reset(Reset));  // open: Qn, preset
  or or_1 (or_1_out, t_ff_4_q, Reset);
endmodule

module fourbit2 (
  input  [3:0] Ain,
  input  [3:0] Bin,
  output Vo,
  output R3,
  output R2,
  output R1,
  output R0
);

  wire fulladder_1_cout, fulladder_2_cout, halfadder_1_cout;

  halfadder halfadder_1 (.InputA(Ain[0]), .InputB(Bin[0]), .numout(R0), .Cout(halfadder_1_cout));
  fulladder fulladder_1 (.Cin(halfadder_1_cout), .A(Ain[1]), .B(Bin[1]), .numout(R1), .Cout(fulladder_1_cout));
  fulladder fulladder_2 (.Cin(fulladder_1_cout), .A(Ain[2]), .B(Bin[2]), .numout(R2), .Cout(fulladder_2_cout));
  fulladder fulladder_3 (.Cin(fulladder_2_cout), .A(Ain[3]), .B(Bin[3]), .numout(R3), .Cout(Vo));
endmodule

module count2 (
  input  Clk,
  input  Reset,
  output [1:0] Cout
);

  wire and_1_out, or_1_out, t_ff_1_q, t_ff_2_q;

  T_Flip_Flop t_ff_1 (.T(1'b1), .clk(Clk), .Q(t_ff_1_q), .reset(or_1_out));  // open: Qn, preset
  D_Flip_Flop d_ff_1 (.D(t_ff_1_q), .clk(Clk), .Q(Cout[0]), .reset(Reset));  // open: Qn, preset
  T_Flip_Flop t_ff_2 (.T(t_ff_1_q), .clk(Clk), .Q(t_ff_2_q), .reset(or_1_out));  // open: Qn, preset
  D_Flip_Flop d_ff_2 (.D(t_ff_2_q), .clk(Clk), .Q(Cout[1]), .reset(Reset));  // open: Qn, preset
  and and_1 (and_1_out, t_ff_1_q, t_ff_2_q);
  or or_1 (or_1_out, and_1_out, Cout[1], Reset);
endmodule
